// Logisim project Doubleadderpart.circ as structural Verilog: 1 circuit, main circuit main
module main (
  input  A1,
  input  A2,
  input  A3,
  input  A4,
  input  B1,
  input  B2,
  input  B3,
  input  B4,
  input  CS0,
  input  CS1,
  input  CS2,
  output C,
  output V,
  output Z,
  output S,
  output F1,
  output F2,
  output F3,
  output F4
);

  wire ADDER_1__15__s4, OR_2__3__1y, OR_2__6__2y, OR_2__8__3y, XiYi_x1, XiYi_x2, XiYi_x3, XiYi_x4, XiYi_y1,
       XiYi_y2, XiYi_y3, XiYi_y4;

  XiYi2_main XiYi (
    .A1(A1), .A2(A2), .A3(A3), .A4(A4), .B1(B1), .B2(B2), .B3(B3), .B4(B4), .CS0(CS0), .CS1(CS1), .CS2(CS2),
    .X1(XiYi_x1), .X2(XiYi_x2), .X3(XiYi_x3), .X4(XiYi_x4), .Y1(XiYi_y1), .Y2(XiYi_y2), .Y3(XiYi_y3),
    .Y4(XiYi_y4));
  _7483 ADDER_2 (
    ._1__A4(1'b0), ._3__A3(1'b0), ._4__B3(1'b0), ._5__Vcc(1'b1), ._6__S2(C), ._7__B2(1'b0), ._8__A2(1'b0),
    ._16__B4(1'b0), ._13__Cin(ADDER_1__15__s4), ._12__GND(1'b0), ._11__B1(XiYi_y4), ._10__A1(XiYi_x4),
    ._9__S1(F4));  // open: _2__S3, _15__S4, _14__Cout
  _7483 ADDER_1 (
    ._1__A4(1'b0), ._2__S3(F3), ._3__A3(XiYi_x3), ._4__B3(XiYi_y3), ._5__Vcc(1'b1), ._6__S2(F2),
    ._7__B2(XiYi_y2), ._8__A2(XiYi_x2), ._16__B4(1'b0), ._15__S4(ADDER_1__15__s4), ._13__Cin(CS2),
    ._12__GND(1'b0), ._11__B1(XiYi_y1), ._10__A1(XiYi_x1), ._9__S1(F1));  // open: _14__Cout
  _7486 XOR_2 (
    ._1__1A(C), ._2__1B(ADDER_1__15__s4), ._3__1Y(V), ._7__GND(1'b0), ._14__Vcc(1'b1));  // open: _4__2A, _5__2B, _6__2Y, _13__4B, _12__4A, _11__4Y, _10__3B, _9__3A, _8__3Y
  _7432 OR_2 (
    ._1__1A(F1), ._2__1B(F2), ._3__1Y(OR_2__3__1y), ._4__2A(OR_2__3__1y), ._5__2B(F3), ._6__2Y(OR_2__6__2y),
    ._7__GND(1'b0), ._14__Vcc(1'b1), ._10__3B(F4), ._9__3A(OR_2__6__2y), ._8__3Y(OR_2__8__3y));  // open: _13__4B, _12__4A, _11__4Y
  not _7404_1 (Z, OR_2__8__3y);

  assign S = F4;

  // Notes on the sheet:
  //   9
  //   8
endmodule
