// Logisim project XiYi2.circ as structural Verilog: 1 circuit, main circuit main
module main (
  input  A1,
  input  A2,
  input  A3,
  input  A4,
  input  B1,
  input  B2,
  input  B3,
  input  B4,
  input  CS0,
  input  CS1,
  input  CS2,
  output X1,
  output X2,
  output X3,
  output X4,
  output Y1,
  output Y2,
  output Y3,
  output Y4
);

  wire AND_1__3__1y, AND_1__6__2y, AND_1__8__3y, NOT_1__2__1y, NOT_1__4__2y, NOT_1__6__3y, NOT_1__10__5y,
       NOT_1__12__6y, OR_1__3__1y, OR_1__6__2y, OR_1__8__3y, OR_1__11__4y, OR_2_out, XOR_1__3__1y,
       XOR_1__6__2y, XOR_1__8__3y, XOR_1__11__4y;

  or OR_2 (OR_2_out, CS2, CS1);
  _7486 XOR_1 (
    ._1__1A(A1), ._2__1B(AND_1__3__1y), ._3__1Y(XOR_1__3__1y), ._4__2A(A2), ._5__2B(AND_1__3__1y),
    ._6__2Y(XOR_1__6__2y), ._7__GND(1'b0), ._14__Vcc(1'b1), ._13__4B(A4), ._12__4A(AND_1__3__1y),
    ._11__4Y(XOR_1__11__4y), ._10__3B(A3), ._9__3A(AND_1__3__1y), ._8__3Y(XOR_1__8__3y));
  _7432 OR_1 (
    ._1__1A(A1), ._2__1B(B1), ._3__1Y(OR_1__3__1y), ._4__2A(A2), ._5__2B(B2), ._6__2Y(OR_1__6__2y),
    ._7__GND(1'b0), ._14__Vcc(1'b1), ._13__4B(A4), ._12__4A(B4), ._11__4Y(OR_1__11__4y), ._10__3B(A3),
    ._9__3A(B3), ._8__3Y(OR_1__8__3y));
  _7408 AND_1 (
    ._1__1A(CS0), ._2__1B(CS2), ._3__1Y(AND_1__3__1y), ._4__2A(NOT_1__2__1y), ._5__2B(CS1),
    ._6__2Y(AND_1__6__2y), ._7__GND(1'b0), ._14__Vcc(1'b1), ._10__3B(CS0), ._9__3A(AND_1__6__2y),
    ._8__3Y(AND_1__8__3y));  // open: _13__4B, _12__4A, _11__4Y
  _7404 NOT_1 (
    ._1__1A(CS2), ._2__1Y(NOT_1__2__1y), ._3__2A(B1), ._4__2Y(NOT_1__4__2y), ._5__3A(B2),
    ._6__3Y(NOT_1__6__3y), ._7__GND(1'b0), ._14__Vcc(1'b1), ._13__6A(B3), ._12__6Y(NOT_1__12__6y),
    ._11__5A(B4), ._10__5Y(NOT_1__10__5y));  // open: _9__4A, _8__4Y
  _74157 MUX_2 (
    ._1__S(CS0), ._2__A1(NOT_1__4__2y), ._3__B1(B1), ._4__Y1(Y1), ._5__A2(NOT_1__6__3y), ._6__B2(B2),
    ._7__Y2(Y2), ._8__GND(1'b0), ._16__Vcc(1'b1), ._15__G(OR_2_out), ._14__A4(NOT_1__10__5y), ._13__B4(B4),
    ._12__Y4(Y4), ._11__A3(NOT_1__12__6y), ._10__B3(B3), ._9__Y3(Y3));
  _74157 MUX_1 (
    ._1__S(AND_1__8__3y), ._2__A1(XOR_1__3__1y), ._3__B1(OR_1__3__1y), ._4__Y1(X1), ._5__A2(XOR_1__6__2y),
    ._6__B2(OR_1__6__2y), ._7__Y2(X2), ._8__GND(1'b0), ._16__Vcc(1'b1), ._15__G(1'b0),
    ._14__A4(XOR_1__11__4y), ._13__B4(OR_1__11__4y), ._12__Y4(X4), ._11__A3(XOR_1__8__3y),
    ._10__B3(OR_1__8__3y), ._9__Y3(X3));

  // Notes on the sheet:
  //   13
  //   12
  //   11
endmodule
