// Logisim project Adder.circ as structural Verilog: 1 circuit, main circuit main
// ADDER
module main (
  input  in_1,
  input  [31:0] A,
  input  [31:0] B,
  input  SIGNA,
  input  in_5,
  input  SIGNB,
  output out_7,
  output [31:0] OUTPUT_OF_WHOLE_ADDER,
  output OUTPUTSIGN
);

  wire comparator_1_eq, comparator_1_lt, multiplexer_3_out, multiplexer_4_out, not_1_out, xnor_1_out,
       xor_1_out;
  wire [31:0] adder_1_out, multiplexer_1_out, negator_1_out, subtractor_1_out;

  Adder #(.width(32)) adder_1 (.a(A), .b(B), .out(adder_1_out), .cin(in_1), .cout(out_7));
  Subtractor #(.width(32)) subtractor_1 (.a(A), .b(B), .out(subtractor_1_out));  // open: bin, bout
  Comparator #(.width(32)) comparator_1 (.a(A), .b(B), .eq(comparator_1_eq), .lt(comparator_1_lt));  // open: gt
  xnor xnor_1 (xnor_1_out, SIGNA, SIGNB);
  Negator #(.width(32)) negator_1 (.in(subtractor_1_out), .out(negator_1_out));
  not not_1 (not_1_out, xnor_1_out);
  Multiplexer #(.width(32)) multiplexer_1 (
    .in0(subtractor_1_out), .in1(negator_1_out), .out(multiplexer_1_out), .sel(comparator_1_lt));  // open: en
  Multiplexer #(.width(32)) multiplexer_2 (
    .in0(adder_1_out), .in1(multiplexer_1_out), .out(OUTPUT_OF_WHOLE_ADDER), .sel(not_1_out));  // open: en
  Multiplexer multiplexer_3 (.in0(SIGNA), .in1(SIGNB), .out(multiplexer_3_out), .sel(comparator_1_lt));  // open: en
  xor xor_1 (xor_1_out, not_1_out, SIGNB);
  Multiplexer multiplexer_4 (
    .in0(multiplexer_3_out), .in1(in_5), .out(multiplexer_4_out), .sel(comparator_1_eq));  // open: en
  Multiplexer multiplexer_5 (.in0(xor_1_out), .in1(multiplexer_4_out), .out(OUTPUTSIGN), .sel(not_1_out));  // open: en

  // Notes on the sheet:
  //   OVERFLOW OF ADDER
endmodule
