// Logisim project FPA.circ as structural Verilog: 4 circuits, main circuit main
module main (
  input  [31:0] A,
  input  [31:0] B,
  output OverFlow,
  output UnderFlow,
  output Denormalized,
  output Nan,
  output InF,
  output Zero_Flag,
  output [8:0] Larger_Exponent,
  output [31:0] Output
);

  wire Input_Handler_larger_sign, Input_Handler_smaller_sign, main_1_outputsign, Normalizer_overflow,
       Normalizer_underflow, not_1_out, not_2_out, R_Nrm_inf, R_Nrm_overflow, special_case_1_out_3;
  wire [8:0] Normalizer_normalizedexponent, R_Nrm_normalized_exponent;
  wire [31:0] Input_Handler_larger_fraction, Input_Handler_shifted_small_fraction,
       main_1_output_of_whole_adder, main_2_rounded_significant, Normalizer_normalizedsignificand,
       OpH_output, R_Nrm_normalized_significand;

  Special_Case special_case_1 (.A(A), .B(B), .out_3(special_case_1_out_3));
  InputHandler Input_Handler (
    .A(A), .B(B), .Larger_Exponant(Larger_Exponent), .Larger_Fraction(Input_Handler_larger_fraction),
    .Larger_Sign(Input_Handler_larger_sign), .Shifted_Small_Fraction(Input_Handler_shifted_small_fraction),
    .Smaller_sign(Input_Handler_smaller_sign));  // open: out_5, Exponant_Difference, Samller_Fraction
  not not_1 (not_1_out, special_case_1_out_3);
  Adder_main main_1 (
    .A(Input_Handler_larger_fraction), .B(Input_Handler_shifted_small_fraction),
    .SIGNA(Input_Handler_larger_sign), .SIGNB(Input_Handler_smaller_sign),
    .OUTPUT_OF_WHOLE_ADDER(main_1_output_of_whole_adder), .OUTPUTSIGN(main_1_outputsign));  // open: out_5
  and and_1 (UnderFlow, not_1_out, Normalizer_underflow);
  Multiplexer #(.width(32), .enable("false")) multiplexer_1 (
    .in0(OpH_output), .in1(B), .out(Output), .sel(special_case_1_out_3));
  _32_bit_ZeroChecker u_32_bit_zerochecker_1 (.Inp(main_1_output_of_whole_adder), .isZero(Zero_Flag));
  Normalizer_main Normalizer (
    .Exponent_Input(Larger_Exponent), .Significand_Input(main_1_output_of_whole_adder),
    .UnderFlow(Normalizer_underflow), .OverFlow(Normalizer_overflow), .Denormalized(Denormalized),
    .NormalizedExponent(Normalizer_normalizedexponent),
    .NormalizedSignificand(Normalizer_normalizedsignificand));
  Rounder_main main_2 (.in_1(Normalizer_normalizedsignificand), .ROUNDED_SIGNIFICANT(main_2_rounded_significant));
  or or_1 (OverFlow, R_Nrm_overflow, Normalizer_overflow);
  not not_2 (not_2_out, UnderFlow);
  Rounded_Normalizer R_Nrm (
    .Exponent_Input(Normalizer_normalizedexponent), .Significand_Input(main_2_rounded_significant),
    .OverFlow(R_Nrm_overflow), .Nan(Nan), .Normalized_Exponent(R_Nrm_normalized_exponent), .InF(R_Nrm_inf),
    .Normalized_Significand(R_Nrm_normalized_significand));
  Output_Handler OpH (
    .Significand(R_Nrm_normalized_significand[29:8]), .Exponent(R_Nrm_normalized_exponent),
    .Sign(main_1_outputsign), .Output(OpH_output));
  and and_2 (InF, not_2_out, R_Nrm_inf);
endmodule

module Output_Handler (
  input  [21:0] Significand,
  input  [8:0] Exponent,
  input  Sign,
  output [31:0] Output
);


  assign Output = {Sign, Exponent, Significand};
endmodule

module Special_Case (
  input  [31:0] A,
  input  [31:0] B,
  output out_3
);

  wire _0_chk_2_iszero, _0_chk_iszero;

  _32_bit_ZeroChecker _0_chk (.Inp({1'b0, A[30:0]}), .isZero(_0_chk_iszero));
  _32_bit_ZeroChecker _0_chk_2 (.Inp({1'b0, B[30:0]}), .isZero(_0_chk_2_iszero));
  and and_1 (out_3, _0_chk_iszero, _0_chk_2_iszero);
endmodule

module _32_bit_ZeroChecker (
  input  [31:0] Inp,
  output isZero
);

  wire or_1_out, or_2_out, or_3_out, or_4_out, or_5_out, or_6_out, or_7_out, or_8_out, or_9_out;

  or or_1 (or_1_out, Inp[0], Inp[1], Inp[2], Inp[3], Inp[4]);
  or or_2 (or_2_out, Inp[5], Inp[6], Inp[7], Inp[8], Inp[9]);
  or or_3 (or_3_out, Inp[10], Inp[11], Inp[12], Inp[13], Inp[14]);
  or or_4 (or_4_out, Inp[15], Inp[16], Inp[17], Inp[18], Inp[19]);
  or or_5 (or_5_out, Inp[20], Inp[21], Inp[22], Inp[23], Inp[24]);
  or or_6 (or_6_out, Inp[25], Inp[26], Inp[27], Inp[28], Inp[29]);
  or or_7 (or_7_out, Inp[30], Inp[31]);
  or or_8 (or_8_out, or_1_out, or_2_out, or_3_out, or_4_out, or_5_out);
  or or_9 (or_9_out, or_6_out, or_7_out);
  nor nor_1 (isZero, or_8_out, or_9_out);
endmodule
