// Logisim project InPutHandler2.circ as structural Verilog: 5 circuits, main circuit 22T32
module main (
  input  [21:0] Fraction,
  output [31:0] _32bitFraction
);

  // Pins of 8 and 10 bits meet at {10{1'b0}}

  assign _32bitFraction = {2'b01, Fraction, {8{1'b0}}};
endmodule

module _22T32 (
  input  [21:0] _22Fraction,
  output [31:0] _32Fraction
);

  // NOT_Gate not_1 is placed but not wired

  assign _32Fraction = {2'b01, _22Fraction, {8{1'b0}}};
endmodule

module Spliter (
  input  [31:0] Input,
  output Sign,
  output [31:0] Fraction,
  output [8:0] Exponent
);

  _22T32 u_22t32_1 (._22Fraction(Input[21:0]), ._32Fraction(Fraction));

  assign Exponent = Input[30:22];
  assign Sign = Input[31];
endmodule

module Exponant_Differentiator (
  input  [8:0] ExponantA,
  input  [8:0] ExponantB,
  input  SignA,
  input  SignB,
  output EA_EB,
  output [8:0] Difference,
  output [8:0] Larger_Exponant,
  output LargerSign,
  output SamllerSign
);

  wire [8:0] multiplexer_2_out;
  wire [9:9] subtractor_1_out;

  Comparator #(.width(9), .mode("unsigned")) comparator_1 (.a(ExponantA), .b(ExponantB), .gt(EA_EB));  // open: eq, lt
  Multiplexer multiplexer_1 (.in0(SignB), .in1(SignA), .out(LargerSign), .sel(EA_EB), .en(1'b1));
  Multiplexer #(.width(9)) multiplexer_2 (
    .in0(ExponantA), .in1(ExponantB), .out(multiplexer_2_out), .sel(EA_EB), .en(1'b1));
  Multiplexer #(.width(9)) multiplexer_3 (
    .in0(ExponantB), .in1(ExponantA), .out(Larger_Exponant), .sel(EA_EB), .en(1'b1));
  Multiplexer multiplexer_4 (.in0(SignA), .in1(SignB), .out(SamllerSign), .sel(EA_EB), .en(1'b1));
  Subtractor #(.width(10)) subtractor_1 (
    .a({1'b0, Larger_Exponant}), .b({1'b0, multiplexer_2_out}), .out({subtractor_1_out[9], Difference}));  // open: bin, bout
endmodule

module InputHandler (
  input  [31:0] InputA,
  input  [31:0] InputB,
  output [31:0] Larger_Fraction,
  output Larger_Sign,
  output [8:0] out_5,
  output [31:0] Shifted_Small_Fraction,
  output [31:0] Samller_Fraction,
  output [8:0] Larger_Exponant,
  output [8:0] Exponant_Difference,
  output Smaller_sign
);

  wire comparator_1_gt, exponant_differentiator_1_ea_eb, spliter_1_sign, spliter_2_sign;
  wire [8:0] spliter_1_exponent, spliter_2_exponent;
  wire [31:0] shifter_1_out, spliter_1_fraction, spliter_2_fraction;

  Spliter spliter_1 (
    .Input(InputA), .Exponent(spliter_1_exponent), .Fraction(spliter_1_fraction), .Sign(spliter_1_sign));
  Spliter spliter_2 (
    .Input(InputB), .Exponent(spliter_2_exponent), .Fraction(spliter_2_fraction), .Sign(spliter_2_sign));
  Exponant_Differentiator exponant_differentiator_1 (
    .ExponantA(spliter_1_exponent), .ExponantB(spliter_2_exponent), .SignA(spliter_1_sign),
    .SignB(spliter_2_sign), .Larger_Exponant(Larger_Exponant), .Difference(Exponant_Difference),
    .EA_EB(exponant_differentiator_1_ea_eb), .LargerSign(Larger_Sign), .SamllerSign(Smaller_sign));
  Multiplexer #(.width(32)) multiplexer_1 (
    .in0(spliter_2_fraction), .in1(spliter_1_fraction), .out(Larger_Fraction),
    .sel(exponant_differentiator_1_ea_eb), .en(1'b1));
  Multiplexer #(.width(32)) multiplexer_2 (
    .in0(spliter_1_fraction), .in1(spliter_2_fraction), .out(Samller_Fraction),
    .sel(exponant_differentiator_1_ea_eb), .en(1'b1));
  Comparator #(.width(9)) comparator_1 (.a(Exponant_Difference), .b(9'h1f), .gt(comparator_1_gt));  // open: eq, lt
  Shifter #(.width(32), .shift("lr")) shifter_1 (
    .in(Samller_Fraction), .\dist (Exponant_Difference[4:0]), .out(shifter_1_out));
  Multiplexer #(.width(32)) multiplexer_3 (
    .in0(shifter_1_out), .in1({32{1'b0}}), .out(Shifted_Small_Fraction), .sel(comparator_1_gt), .en(1'b1));

  assign out_5 = 9'h1f;
endmodule
