// Logisim project Normalizer.circ as structural Verilog: 7 circuits, main circuit main
module main (
  input  [8:0] Exponent_Input,
  input  [31:0] Significand_Input,
  output [8:0] NormalizedExponent,
  output [31:0] NormalizedSignificand,
  output UnderFlow,
  output OverFlow,
  output Denormalized
);

  wire adder_subtractor_lib_1_denormalized, adder_subtractor_lib_1_overflow,
       adder_subtractor_lib_1_underflow, and_1_out, and_2_out, n32_bit_zero_checker_1_iszero,
       priority_encoder_1_en_out, xor_1_out, zero_checker_1_iszero;
  wire [4:0] multiplexer_1_out, priority_encoder_1_out, subtractor_1_out;
  wire [8:0] adder_subtractor_lib_1_output_exponent;
  wire [31:0] shifter_1_output;

  xor xor_1 (xor_1_out, Significand_Input[31], 1'b1);
  and and_1 (and_1_out, xor_1_out, priority_encoder_1_en_out);
  Priority_Encoder #(.select(5)) priority_encoder_1 (
    .in0(Significand_Input[0]), .in1(Significand_Input[1]), .in2(Significand_Input[2]),
    .in3(Significand_Input[3]), .in4(Significand_Input[4]), .in5(Significand_Input[5]),
    .in6(Significand_Input[6]), .in7(Significand_Input[7]), .in8(Significand_Input[8]),
    .in9(Significand_Input[9]), .in10(Significand_Input[10]), .in11(Significand_Input[11]),
    .in12(Significand_Input[12]), .in13(Significand_Input[13]), .in14(Significand_Input[14]),
    .in15(Significand_Input[15]), .in16(Significand_Input[16]), .in17(Significand_Input[17]),
    .in18(Significand_Input[18]), .in19(Significand_Input[19]), .in20(Significand_Input[20]),
    .in21(Significand_Input[21]), .in22(Significand_Input[22]), .in23(Significand_Input[23]),
    .in24(Significand_Input[24]), .in25(Significand_Input[25]), .in26(Significand_Input[26]),
    .in27(Significand_Input[27]), .in28(Significand_Input[28]), .in29(Significand_Input[29]),
    .in30(Significand_Input[30]), .in31(1'b0), .out(priority_encoder_1_out),
    .en_out(priority_encoder_1_en_out), .en_in(1'b1));  // open: gs
  Subtractor #(.width(5)) subtractor_1 (
    .a(5'b11110), .b(priority_encoder_1_out), .out(subtractor_1_out));  // open: bin, bout
  Multiplexer #(.width(5), .disabled(0), .enable("false")) multiplexer_1 (
    .in0(subtractor_1_out), .in1(5'b00001), .out(multiplexer_1_out), .sel(Significand_Input[31]));
  Shifter shifter_1 (
    .Input(Significand_Input), .SftAmt(multiplexer_1_out), .Left_Right(Significand_Input[31]),
    .Output(shifter_1_output));
  Multiplexer #(.width(9), .disabled(0), .enable("false")) multiplexer_2 (
    .in0(adder_subtractor_lib_1_output_exponent), .in1({9{1'b0}}), .out(NormalizedExponent), .sel(and_1_out));
  zero_checker zero_checker_1 (.Exponent(Exponent_Input), .isZero(zero_checker_1_iszero));
  _32_bit_Zero_checker u_32_bit_zero_checker_1 (.Inp(Significand_Input), .isZero(n32_bit_zero_checker_1_iszero));
  Adder_Subtractor_Lib adder_subtractor_lib_1 (
    .Input_Exponent(Exponent_Input), .add_sub_amount(multiplexer_1_out),
    .Denormalized(adder_subtractor_lib_1_denormalized), .Add_Sub(Significand_Input[31]),
    .OverFlow(adder_subtractor_lib_1_overflow), .UnderFlow(adder_subtractor_lib_1_underflow),
    .Output_Exponent(adder_subtractor_lib_1_output_exponent));
  and and_2 (and_2_out, zero_checker_1_iszero, n32_bit_zero_checker_1_iszero);
  Multiplexer #(.enable("false")) multiplexer_3 (
    .in0(adder_subtractor_lib_1_denormalized), .in1(1'b0), .out(Denormalized), .sel(and_2_out));
  Multiplexer #(.width(32), .disabled(0), .enable("false")) multiplexer_4 (
    .in0(shifter_1_output), .in1({32{1'b0}}), .out(NormalizedSignificand), .sel(and_1_out));
  Multiplexer #(.disabled(0), .enable("false")) multiplexer_5 (
    .in0(adder_subtractor_lib_1_underflow), .in1(1'b0), .out(UnderFlow), .sel(and_1_out));
  Multiplexer #(.disabled(0), .enable("false")) multiplexer_6 (
    .in0(adder_subtractor_lib_1_overflow), .in1(1'b0), .out(OverFlow), .sel(and_1_out));
endmodule

module Shifter (
  input  [31:0] Input,
  input  [4:0] SftAmt,
  input  Left_Right,
  output [31:0] Output
);

  wire [31:0] arbitary_rightshifter_1_output, arbitrary_leftshifter_1_out_3;

  arbitrary_leftShifter arbitrary_leftshifter_1 (.in_1(Input), .in_2(SftAmt), .out_3(arbitrary_leftshifter_1_out_3));
  arbitary_rightShifter arbitary_rightshifter_1 (
    .\input (Input), .Shift_Amount(SftAmt), .\output (arbitary_rightshifter_1_output));
  Multiplexer #(.width(32), .disabled(0), .enable("false")) multiplexer_1 (
    .in0(arbitrary_leftshifter_1_out_3), .in1(arbitary_rightshifter_1_output), .out(Output), .sel(Left_Right));
endmodule

// A/S
module Adder_Subtractor_Lib (
  input  [8:0] Input_Exponent,
  input  [4:0] add_sub_amount,
  input  Add_Sub,
  output UnderFlow,
  output Denormalized,
  output [8:0] Output_Exponent,
  output OverFlow
);

  wire and_1_out, not_1_out, not_2_out, one_checker_1_isone, or_1_out, zero_checker_1_iszero;
  wire [8:0] adder_1_out, subtractor_1_out;

  Subtractor #(.width(9)) subtractor_1 (
    .a(Input_Exponent), .b({4'b0000, add_sub_amount}), .out(subtractor_1_out), .bin(1'b0), .bout(UnderFlow));
  Adder #(.width(9)) adder_1 (
    .a(Input_Exponent), .b({4'b0000, add_sub_amount}), .out(adder_1_out), .cin(1'b0), .cout(OverFlow));
  not not_1 (not_1_out, UnderFlow);
  or or_1 (or_1_out, OverFlow, one_checker_1_isone);
  and and_1 (and_1_out, not_1_out, zero_checker_1_iszero);
  zero_checker zero_checker_1 (.Exponent(Output_Exponent), .isZero(zero_checker_1_iszero));
  One_Checker one_checker_1 (.Exponent(Output_Exponent), .isOne(one_checker_1_isone));
  not not_2 (not_2_out, Add_Sub);
  Multiplexer #(.width(9), .disabled(0), .enable("false")) multiplexer_1 (
    .in0(subtractor_1_out), .in1(adder_1_out), .out(Output_Exponent), .sel(Add_Sub));
  // AND_Gate and_2 has open pins: in0=Add_Sub, in1=or_1_out, out=open
  and and_3 (Denormalized, not_2_out, and_1_out);
endmodule

// ZeroChk
module zero_checker (
  input  [8:0] Exponent,
  output isZero
);

  wire or_1_out, or_2_out;

  or or_1 (or_1_out, Exponent[0], Exponent[1], Exponent[2], Exponent[3], Exponent[4]);
  or or_2 (or_2_out, Exponent[5], Exponent[6], Exponent[7], Exponent[8]);
  nor nor_1 (isZero, or_1_out, or_2_out);
endmodule

// OneChk
module One_Checker (
  input  [8:0] Exponent,
  output isOne
);

  wire and_1_out, and_2_out;

  and and_1 (and_1_out, Exponent[0], Exponent[1], Exponent[2], Exponent[3], Exponent[4]);
  and and_2 (and_2_out, Exponent[5], Exponent[6], Exponent[7], Exponent[8]);
  and and_3 (isOne, and_1_out, and_2_out);
endmodule

module Rounded_Normalizer (
  input  [8:0] Exponent_Input,
  input  [31:0] Significand_Input,
  output Nan,
  output [8:0] Normalized_Exponent,
  output OverFlow,
  output InF,
  output [31:0] Normalized_Significand
);

  wire n32_bit_zero_checker_1_iszero, not_1_out, not_2_out, one_checker_1_isone;
  wire [31:0] n1_bit_rightshifter_1_out_3;

  Adder #(.width(9)) adder_1 (
    .a(Exponent_Input), .b({9{1'b0}}), .out(Normalized_Exponent), .cin(Significand_Input[31]), .cout(OverFlow));
  _1_bit_rightShifter u_1_bit_rightshifter_1 (
    .in_1(Significand_Input), .in_2(1'b1), .out_3(n1_bit_rightshifter_1_out_3));
  One_Checker one_checker_1 (.Exponent(Normalized_Exponent), .isOne(one_checker_1_isone));
  Multiplexer #(.width(32), .disabled(0), .enable("false")) multiplexer_1 (
    .in0(Significand_Input), .in1(n1_bit_rightshifter_1_out_3), .out(Normalized_Significand),
    .sel(Significand_Input[31]));
  not not_1 (not_1_out, OverFlow);
  and and_1 (Nan, not_1_out, one_checker_1_isone, not_2_out);
  not not_2 (not_2_out, n32_bit_zero_checker_1_iszero);
  _32_bit_Zero_checker u_32_bit_zero_checker_1 (.Inp(Normalized_Significand), .isZero(n32_bit_zero_checker_1_iszero));
  and u_InF (InF, one_checker_1_isone, not_1_out, n32_bit_zero_checker_1_iszero);
endmodule

module _32_bit_Zero_checker (
  input  [31:0] Inp,
  output isZero
);

  wire or_1_out, or_2_out, or_3_out, or_4_out, or_5_out, or_6_out, or_7_out, or_8_out, or_9_out;

  or or_1 (or_1_out, Inp[0], Inp[1], Inp[2], Inp[3], Inp[4]);
  or or_2 (or_2_out, Inp[5], Inp[6], Inp[7], Inp[8], Inp[9]);
  or or_3 (or_3_out, Inp[10], Inp[11], Inp[12], Inp[13], Inp[14]);
  or or_4 (or_4_out, Inp[15], Inp[16], Inp[17], Inp[18], Inp[19]);
  or or_5 (or_5_out, Inp[20], Inp[21], Inp[22], Inp[23], Inp[24]);
  or or_6 (or_6_out, Inp[25], Inp[26], Inp[27], Inp[28], Inp[29]);
  or or_7 (or_7_out, or_1_out, or_2_out, or_3_out, or_4_out, or_5_out);
  or or_8 (or_8_out, Inp[30], Inp[31]);
  or or_9 (or_9_out, or_6_out, or_8_out);
  nor nor_1 (isZero, or_7_out, or_9_out);
endmodule
