// Logisim project Rounder.circ as structural Verilog: 1 circuit, main circuit main
// ROUNDER
module main (
  input  [31:0] in_1,
  output [31:0] ROUNDED_SIGNIFICANT
);

  wire and_1_out, comparator_1_eq, comparator_1_gt, or_1_out;

  Comparator #(.width(3), .mode("unsigned")) comparator_1 (
    .a(in_1[7:5]), .b(3'b100), .gt(comparator_1_gt), .eq(comparator_1_eq));  // open: lt
  and and_1 (and_1_out, in_1[8], comparator_1_eq);
  Adder #(.width(24)) adder_1 (
    .a(in_1[31:8]), .b({24{1'b0}}), .out(ROUNDED_SIGNIFICANT[31:8]), .cin(or_1_out));  // open: cout
  or or_1 (or_1_out, and_1_out, comparator_1_gt);

  assign ROUNDED_SIGNIFICANT[7:0] = {8{1'b0}};

  // Notes on the sheet:
  //   SIGNIFICAND
endmodule
