// Logisim project leftShifterLib.circ as structural Verilog: 7 circuits, main circuit Subtractor
module Subtractor (
  input  [10:0] Ea,
  input  [19:0] Fa,
  input  [10:0] Eb,
  input  [19:0] Fb,
  input  [10:0] in_5,
  output [10:0] out_6,
  output [19:0] Smaller,
  output [19:0] Greater
);

  wire comparator_1_eq, comparator_1_gt, comparator_1_lt, or_1_out;

  Subtractor_part #(.width(11)) subtractor_1 (.a(Ea), .b(Eb), .out(out_6));  // open: bin, bout
  Comparator #(.width(11)) comparator_1 (
    .a(out_6), .b(in_5), .gt(comparator_1_gt), .eq(comparator_1_eq), .lt(comparator_1_lt));
  or or_1 (or_1_out, comparator_1_eq, comparator_1_lt);
  Multiplexer #(.width(20)) multiplexer_1 (.in0(Fb), .in1(Fa), .out(Smaller), .sel(or_1_out), .en(1'b1));
  Multiplexer #(.width(20)) multiplexer_2 (.in0(Fb), .in1(Fa), .out(Greater), .sel(comparator_1_gt), .en(1'b1));
endmodule

// 1
module _1bit_leftShifter (
  input  [31:0] F,
  input  S,
  output [31:0] out_3
);

  Multiplexer #(.width(32)) multiplexer_1 (.in0(F), .in1({F[30:0], 1'b0}), .out(out_3), .sel(S), .en(1'b1));
endmodule

// 2
module _2bit_leftShifter (
  input  [31:0] F,
  input  S,
  output [31:0] out_3
);

  Multiplexer #(.width(32)) multiplexer_1 (.in0(F), .in1({F[29:0], 2'b00}), .out(out_3), .sel(S), .en(1'b1));
endmodule

// 4
module _4bit_leftShifter (
  input  [31:0] F,
  input  S,
  output [31:0] out_3
);

  Multiplexer #(.width(32)) multiplexer_1 (.in0(F), .in1({F[27:0], 4'b0000}), .out(out_3), .sel(S), .en(1'b1));
endmodule

// 8
module _8bit_leftShifter (
  input  [31:0] F,
  input  S,
  output [31:0] out_3
);

  Multiplexer #(.width(32)) multiplexer_1 (.in0(F), .in1({F[23:0], {8{1'b0}}}), .out(out_3), .sel(S), .en(1'b1));
endmodule

// 16
module _16bit_leftShifter (
  input  S,
  input  [31:0] F,
  output [31:0] out_3
);

  Multiplexer #(.width(32)) multiplexer_1 (.in0(F), .in1({F[15:0], {16{1'b0}}}), .out(out_3), .sel(S), .en(1'b1));
endmodule

module arbitrary_leftShifter (
  input  [31:0] in_1,
  input  [4:0] in_2,
  output [31:0] out_3
);

  wire [31:0] n1bit_leftshifter_1_out_3, n2bit_leftshifter_1_out_3, n4bit_leftshifter_1_out_3,
       n8bit_leftshifter_1_out_3;

  _1bit_leftShifter u_1bit_leftshifter_1 (.F(in_1), .S(in_2[0]), .out_3(n1bit_leftshifter_1_out_3));
  _2bit_leftShifter u_2bit_leftshifter_1 (
    .F(n1bit_leftshifter_1_out_3), .S(in_2[1]), .out_3(n2bit_leftshifter_1_out_3));
  _4bit_leftShifter u_4bit_leftshifter_1 (
    .F(n2bit_leftshifter_1_out_3), .S(in_2[2]), .out_3(n4bit_leftshifter_1_out_3));
  _8bit_leftShifter u_8bit_leftshifter_1 (
    .F(n4bit_leftshifter_1_out_3), .S(in_2[3]), .out_3(n8bit_leftshifter_1_out_3));
  _16bit_leftShifter u_16bit_leftshifter_1 (.F(n8bit_leftshifter_1_out_3), .S(in_2[4]), .out_3(out_3));
endmodule
