// Logisim project EX_MEM_Regi.circ as structural Verilog: 1 circuit, main circuit main
module main (
  input  [3:0] MemToReg_MW_MR_RW,
  input  [1:0] BN_B,
  input  [7:0] Label_Address,
  input  Zero_flag,
  input  [7:0] ALU_Result,
  input  [3:0] RD,
  input  [7:0] Data_Memory,
  input  clock,
  input  clear,
  output [3:0] MemToReg_MW_MR_RW_2,
  output MemToReg,
  output MemWrite,
  output MemRead,
  output RegWrite,
  output [1:0] BN_B_2,
  output [7:0] Level_Adress,
  output Zero_Flag_2,
  output [7:0] ALU_Result_2,
  output [3:0] RD_2,
  output [7:0] Data_Memory_2
);

  Register #(.width(27)) register_1 (
    .D({RD, ALU_Result, Zero_flag, Label_Address, BN_B, MemToReg_MW_MR_RW}), .en(1'b1),
    .Q({RD_2, ALU_Result_2, Zero_Flag_2, Level_Adress, BN_B_2, MemToReg_MW_MR_RW_2[3], MemRead, MemToReg_MW_MR_RW_2[1], MemToReg}),
    .clk(clock), .clr(clear));
  Register register_2 (.D(Data_Memory), .en(1'b1), .Q(Data_Memory_2), .clk(clock), .clr(clear));

  assign {MemToReg_MW_MR_RW_2[2], MemToReg_MW_MR_RW_2[0]} = {MemRead, MemToReg};
  assign MemWrite = MemToReg_MW_MR_RW_2[1];
  assign RegWrite = MemToReg_MW_MR_RW_2[3];
endmodule
