// Logisim project Fwding_Unit.circ as structural Verilog: 1 circuit, main circuit Fwding UNit
module Fwding_UNit (
  input  EX_MEM_RegWrite,
  input  [3:0] EX_MEM_Destination_Reg,
  input  [3:0] ID_EX_ReadRegister1,
  input  [3:0] ID_EX_ReadRegister2,
  input  MEM_WB_RegWrite,
  input  [3:0] MEM_WB_Destination_Reg,
  output [1:0] FWD_A,
  output [1:0] FWD_B
);

  wire comparator_1_eq, comparator_2_eq, comparator_3_eq, comparator_4_eq, comparator_5_eq, comparator_6_eq,
       not_1_out, not_2_out, not_3_out, not_4_out;

  Comparator #(.width(4)) comparator_1 (.a(4'b0000), .b(EX_MEM_Destination_Reg), .eq(comparator_1_eq));  // open: gt, lt
  Comparator #(.width(4)) comparator_2 (
    .a(EX_MEM_Destination_Reg), .b(ID_EX_ReadRegister1), .eq(comparator_2_eq));  // open: gt, lt
  Comparator #(.width(4)) comparator_3 (
    .a(EX_MEM_Destination_Reg), .b(ID_EX_ReadRegister2), .eq(comparator_3_eq));  // open: gt, lt
  not not_1 (not_1_out, comparator_4_eq);
  Comparator #(.width(4)) comparator_4 (.a(4'b0000), .b(MEM_WB_Destination_Reg), .eq(comparator_4_eq));  // open: gt, lt
  Comparator #(.width(4)) comparator_5 (
    .a(MEM_WB_Destination_Reg), .b(ID_EX_ReadRegister1), .eq(comparator_5_eq));  // open: gt, lt
  Comparator #(.width(4)) comparator_6 (
    .a(MEM_WB_Destination_Reg), .b(ID_EX_ReadRegister2), .eq(comparator_6_eq));  // open: gt, lt
  not not_2 (not_2_out, comparator_1_eq);
  and and_1 (FWD_A[1], EX_MEM_RegWrite, not_2_out, comparator_2_eq);
  and and_2 (FWD_B[1], EX_MEM_RegWrite, not_2_out, comparator_3_eq);
  not not_3 (not_3_out, FWD_A[1]);
  not not_4 (not_4_out, FWD_B[1]);
  and and_3 (FWD_A[0], not_3_out, MEM_WB_RegWrite, not_1_out, comparator_5_eq);
  and and_4 (FWD_B[0], not_4_out, MEM_WB_RegWrite, not_1_out, comparator_6_eq);
endmodule
