// Logisim project Hazard_Detection.circ as structural Verilog: 1 circuit, main circuit main
// Hazard Detection Unit
module main (
  input  ID_EX_MemRead,
  input  [3:0] ID_EX_RegRt,
  input  [3:0] IF_ID_RegRs,
  input  [3:0] IF_ID_RegRt,
  output out_5
);

  wire comparator_1_eq, comparator_2_eq, or_1_out;

  Comparator #(.width(4), .mode("unsigned")) comparator_1 (
    .a(ID_EX_RegRt), .b(IF_ID_RegRs), .eq(comparator_1_eq));  // open: gt, lt
  Comparator #(.width(4), .mode("unsigned")) comparator_2 (
    .a(ID_EX_RegRt), .b(IF_ID_RegRt), .eq(comparator_2_eq));  // open: gt, lt
  or or_1 (or_1_out, comparator_1_eq, comparator_2_eq);
  and and_1 (out_5, ID_EX_MemRead, or_1_out);
endmodule
