// Logisim project Hazard_Detection_Branching.circ as structural Verilog: 1 circuit, main circuit main
// Hazard Detection Unit
module main (
  input  ID_EX_MemRead,
  input  [3:0] ID_EX_RegRt,
  input  [3:0] IF_ID_RegRs,
  input  [3:0] IF_ID_RegRt,
  input  IF_ID_Be,
  input  IF_ID_Bne,
  input  [3:0] ID_EX_RegRd,
  input  [3:0] IF_ID_RegRs_2,
  input  [3:0] IF_ID_RegRt_2,
  input  EX_MEM_MemRead,
  input  [3:0] EX_MEM_RegRt,
  input  [3:0] IF_ID_RegRs_3,
  input  [3:0] IF_ID_RegRt_3,
  output Load_Use_and_branch_after_load,
  output Stall,
  output branch_after_add_i,
  output branch_after_after_load
);

  wire comparator_1_eq, comparator_2_eq, comparator_3_eq, comparator_4_eq, comparator_5_eq, comparator_6_eq,
       or_1_out, or_2_out, or_3_out, or_4_out;

  or or_1 (or_1_out, IF_ID_Be, IF_ID_Bne);
  Comparator #(.width(4), .mode("unsigned")) comparator_1 (
    .a(ID_EX_RegRt), .b(IF_ID_RegRs), .eq(comparator_1_eq));  // open: gt, lt
  Comparator #(.width(4), .mode("unsigned")) comparator_2 (
    .a(ID_EX_RegRt), .b(IF_ID_RegRt), .eq(comparator_2_eq));  // open: gt, lt
  Comparator #(.width(4), .mode("unsigned")) comparator_3 (
    .a(ID_EX_RegRd), .b(IF_ID_RegRs_2), .eq(comparator_3_eq));  // open: gt, lt
  Comparator #(.width(4), .mode("unsigned")) comparator_4 (
    .a(ID_EX_RegRd), .b(IF_ID_RegRt_2), .eq(comparator_4_eq));  // open: gt, lt
  Comparator #(.width(4), .mode("unsigned")) comparator_5 (
    .a(EX_MEM_RegRt), .b(IF_ID_RegRs_3), .eq(comparator_5_eq));  // open: gt, lt
  Comparator #(.width(4), .mode("unsigned")) comparator_6 (
    .a(EX_MEM_RegRt), .b(IF_ID_RegRt_3), .eq(comparator_6_eq));  // open: gt, lt
  or or_2 (or_2_out, comparator_1_eq, comparator_2_eq);
  or or_3 (or_3_out, comparator_3_eq, comparator_4_eq);
  or or_4 (or_4_out, comparator_5_eq, comparator_6_eq);
  and and_1 (Load_Use_and_branch_after_load, ID_EX_MemRead, or_2_out);
  and and_2 (branch_after_add_i, or_1_out, or_3_out);
  and and_3 (branch_after_after_load, EX_MEM_MemRead, or_4_out);
  or or_5 (Stall, Load_Use_and_branch_after_load, branch_after_add_i, branch_after_after_load);

  // Notes on the sheet:
  //   load_use
  //   branching data hazard
  //   it also solves store after load surprisingly :3
endmodule
