// Logisim project ID_EX_Regi.circ as structural Verilog: 1 circuit, main circuit ID/EX
module ID_EX (
  input  [7:0] Next_Pc,
  input  [8:0] ALUSrc_BN_B_MemToReg_MW_MR_RW_RD_S,
  input  [11:0] RS_RT_RD,
  input  [7:0] Value_of_RS,
  input  [7:0] Value_of_Rd_rt,
  input  [7:0] Value_of_im,
  input  [2:0] ALU_OP,
  input  CLR,
  input  Clock,
  output [7:0] Next_Pc_2,
  output [8:0] ALUSrc_BN_B_MemToReg_MW_MR_RW_RD_S_2,
  output ALUSrc,
  output [5:0] mem,
  output reg_destination,
  output Shift,
  output [11:0] RS_RT_RD_2,
  output [3:0] rs_reg,
  output [3:0] rt_reg,
  output [3:0] rd_reg,
  output [23:0] VALUES_RS_RD_RT_IM,
  output [7:0] rs,
  output [7:0] rt,
  output [7:0] im,
  output [2:0] ALU_OP_2
);

  Register #(.width(29)) register_1 (
    .D({RS_RT_RD, ALUSrc_BN_B_MemToReg_MW_MR_RW_RD_S, Next_Pc}), .en(1'b1),
    .Q({rd_reg, RS_RT_RD_2[7:4], rs_reg, ALUSrc_BN_B_MemToReg_MW_MR_RW_RD_S_2[8:1], ALUSrc, Next_Pc_2}),
    .clk(Clock), .clr(CLR));
  Register register_2 (.D(Value_of_RS), .en(1'b1), .Q(rs), .clk(Clock), .clr(CLR));
  Register register_3 (.D(Value_of_Rd_rt), .en(1'b1), .Q(rt), .clk(Clock), .clr(CLR));
  Register register_4 (.D(Value_of_im), .en(1'b1), .Q(im), .clk(Clock), .clr(CLR));
  Register #(.width(3)) register_5 (.D(ALU_OP), .en(1'b1), .Q(ALU_OP_2), .clk(Clock), .clr(CLR));

  assign ALUSrc_BN_B_MemToReg_MW_MR_RW_RD_S_2[0] = ALUSrc;
  assign mem = ALUSrc_BN_B_MemToReg_MW_MR_RW_RD_S_2[6:1];
  assign reg_destination = ALUSrc_BN_B_MemToReg_MW_MR_RW_RD_S_2[7];
  assign {RS_RT_RD_2[11:8], RS_RT_RD_2[3:0]} = {rd_reg, rs_reg};
  assign rt_reg = RS_RT_RD_2[7:4];
  assign Shift = ALUSrc_BN_B_MemToReg_MW_MR_RW_RD_S_2[8];
  assign VALUES_RS_RD_RT_IM = {im, rt, rs};

  // Notes on the sheet:
  //   Register Numbers
  //   RD= RegDst S = Shift 
  //   J means Jump , MR = MEMORY Read  ,BN = bneq,B= beq
endmodule
