// Logisim project Mem_Wb_regi.circ as structural Verilog: 1 circuit, main circuit main
// Mem/WB
module main (
  input  MemToReg_RW,
  input  RW,
  input  [7:0] Data_Memory,
  input  [7:0] ALU_Result,
  input  clear,
  input  clock,
  input  [3:0] RD,
  output MemToReg_RW_2,
  output RW_2,
  output [7:0] Data_Memory_2,
  output [7:0] ALU_Result_2,
  output [3:0] RD_2
);

  Register #(.width(2)) register_1 (
    .D({RW, MemToReg_RW}), .en(1'b1), .Q({RW_2, MemToReg_RW_2}), .clk(clock), .clr(clear));
  Register register_2 (.D(Data_Memory), .en(1'b1), .Q(Data_Memory_2), .clk(clock), .clr(clear));
  Register #(.width(12)) register_3 (
    .D({RD, ALU_Result}), .en(1'b1), .Q({RD_2, ALU_Result_2}), .clk(clock), .clr(clear));
endmodule
