// Logisim project Project_No_PipeLine.circ as structural Verilog
module main (
  input  Clr,
  output [3:0] Opcode,
  output [3:0] src1,
  output [19:0] Read_Adress,
  output [7:0] Result,
  output [7:0] PC,
  output [3:0] src2,
  output [7:0] B,
  output [7:0] A_Read_Data,
  output [3:0] dst,
  output [3:0] out_11,
  output [7:0] Read_Data_2,
  output [7:0] Write_Data,
  output [7:0] zero,
  output [7:0] sp,
  output [7:0] t0,
  output [7:0] t4,
  output [7:0] t1,
  output [7:0] t3,
  output [7:0] t2
);

  wire alu_8_by_art_1_p4, and_1_out, and_2_out, Clock_Pulse_out, control_1_alusrc, control_1_beq,
       control_1_bneq, control_1_jump, control_1_memread, control_1_memtoreg, control_1_memwrite,
       control_1_regdst, control_1_regwrite, control_1_shift, not_1_out, not_2_out;
  wire [1:0] priority_encoder_1_out;
  wire [2:0] control_1_aluop;
  wire [3:0] multiplexer_1_out;
  wire [7:0] adder_1_out, adder_2_out, multiplexer_4_out, multiplexer_5_out, multiplexer_7_out, ram_1_data;

  Register_part register_1 (.D(multiplexer_7_out), .Q(PC), .clk(Clock_Pulse_out), .clr(Clr));  // open: en
  Clock Clock_Pulse (.out(Clock_Pulse_out));
  Adder adder_1 (.a(8'h1), .b(PC), .out(adder_1_out), .cin(1'b0));  // open: cout
  ROM #(.dataWidth(20)) rom_1 (.addr(PC), .data({Opcode, Read_Adress[15:4], out_11}));  // open: sel
  Multiplexer #(.width(4), .enable("false")) multiplexer_1 (
    .in0(Read_Adress[7:4]), .in1(4'b0000), .out(multiplexer_1_out), .sel(control_1_shift));
  Multiplexer #(.width(4), .enable("false")) multiplexer_2 (
    .in0(Read_Adress[11:8]), .in1(Read_Adress[7:4]), .out(dst), .sel(control_1_regdst));
  Control control_1 (
    .OpCode(Opcode), .ALUOp(control_1_aluop), .ALUSrc(control_1_alusrc), .Bneq(control_1_bneq),
    .Beq(control_1_beq), .MemToReg(control_1_memtoreg), .MemWrite(control_1_memwrite),
    .MemRead(control_1_memread), .RegWrite(control_1_regwrite), .RegDst(control_1_regdst),
    .Shift(control_1_shift), .Jump(control_1_jump));
  Adder adder_2 (.a(adder_1_out), .b({multiplexer_1_out, out_11}), .out(adder_2_out));  // open: cin, cout
  Register register_2 (
    .Write_Data(Write_Data), .Read_Register_2(Read_Adress[11:8]), .Read_Register_1(Read_Adress[15:12]),
    .Write_Register(dst), .CLK(Clock_Pulse_out), .Write_Signal(control_1_regwrite), .Clear(Clr), .zero(zero),
    .t0(t0), .t1(t1), .t2(t2), .t3(t3), .t4(t4), .sp(sp), .Read_data_1(A_Read_Data), .Read_data_2(Read_Data_2));
  Multiplexer #(.width(8), .enable("false")) multiplexer_3 (
    .in0(Read_Data_2), .in1({multiplexer_1_out, out_11}), .out(B), .sel(control_1_alusrc));
  Multiplexer #(.width(8), .enable("false")) multiplexer_4 (
    .in0(B), .in1(A_Read_Data), .out(multiplexer_4_out), .sel(control_1_shift));
  Multiplexer #(.width(8), .enable("false")) multiplexer_5 (
    .in0(A_Read_Data), .in1(B), .out(multiplexer_5_out), .sel(control_1_shift));
  // ALU_8_by_ART alu_8_by_art_1: pin names not known; wires that end beside it: multiplexer_5_out, multiplexer_4_out, control_1_aluop, alu_8_by_art_1_p4, Result
  not not_1 (not_1_out, alu_8_by_art_1_p4);
  and and_1 (and_1_out, control_1_bneq, not_1_out);
  and and_2 (and_2_out, control_1_beq, alu_8_by_art_1_p4);
  not not_2 (not_2_out, Clock_Pulse_out);
  Priority_Encoder #(.select(2)) priority_encoder_1 (
    .in0(1'b1), .in1(and_1_out), .in2(and_2_out), .in3(control_1_jump), .out(priority_encoder_1_out));  // open: gs, en_out, en_in
  Multiplexer #(.width(8), .enable("false")) multiplexer_6 (
    .in0(Result), .in1(ram_1_data), .out(Write_Data), .sel(control_1_memtoreg));
  RAM #(.bus("separate")) ram_1 (
    .addr(Result), .din(Read_Data_2), .data(ram_1_data), .str(control_1_memwrite), .clk(not_2_out),
    .ld(control_1_memread), .clr(Clr));  // open: sel
  Multiplexer #(.select(2), .width(8), .enable("false")) multiplexer_7 (
    .in0(adder_1_out), .in1(adder_2_out), .in2(adder_2_out), .in3(Read_Adress[15:8]),
    .out(multiplexer_7_out), .sel(priority_encoder_1_out));

  assign {Read_Adress[19:16], Read_Adress[3:0]} = {Opcode, out_11};
  assign src1 = Read_Adress[15:12];
  assign src2 = Read_Adress[11:8];

  // Notes on the sheet:
  //   contents of rom_1 (hex, n*v repeats v):
  //   1010a 10201 d1209 10202 d1209 10201 10301 10502 42340 40320 40430 15501 951fb a0f00 10401 56400
  //   e6601 34014 56100 e6601 b1055 56500 e6601 555a2 56500 e6601 652a2 56200 e6601 12388 56300 e6601
  //   e3481 c4340 56400 e6601 10146 10255 71230 56300 e6601 34fe 56400 e6601 10480 105aa f4520 56200 e6601
  //   223ff 56300 e6601 a3400
  //   Clear Register
endmodule

module Register (
  input  [3:0] Write_Register,
  input  [7:0] Write_Data,
  input  CLK,
  input  Write_Signal,
  input  Clear,
  input  [3:0] Read_Register_2,
  input  [3:0] Read_Register_1,
  output [7:0] Read_data_1,
  output [7:0] Read_data_2,
  output [7:0] sp,
  output [7:0] zero,
  output [7:0] t2,
  output [7:0] t4,
  output [7:0] t0,
  output [7:0] t3,
  output [7:0] t1
);

  wire and_1_out, and_2_out, and_3_out, and_4_out, and_5_out, and_6_out, and_7_out, decoder_1_out0,
       decoder_1_out1, decoder_1_out2, decoder_1_out3, decoder_1_out4, decoder_1_out5, decoder_1_out6,
       multiplexer_1_out, multiplexer_3_out;
  wire [7:0] multiplexer_2_out;

  Decoder #(.select(4), .enable("false")) decoder_1 (
    .out0(decoder_1_out0), .out1(decoder_1_out1), .out2(decoder_1_out2), .out3(decoder_1_out3),
    .out4(decoder_1_out4), .out5(decoder_1_out5), .out6(decoder_1_out6), .sel(Write_Register));  // open: out7, out8, out9, out10, out11, out12, out13, out14, out15
  and and_1 (and_1_out, decoder_1_out0, 1'b0);
  and and_2 (and_2_out, decoder_1_out1, Write_Signal);
  and and_3 (and_3_out, decoder_1_out2, Write_Signal);
  and and_4 (and_4_out, decoder_1_out3, Write_Signal);
  and and_5 (and_5_out, decoder_1_out4, Write_Signal);
  and and_6 (and_6_out, decoder_1_out5, Write_Signal);
  and and_7 (and_7_out, decoder_1_out6, Write_Signal);
  Multiplexer #(.enable("false")) multiplexer_1 (.in0(and_7_out), .in1(Clear), .out(multiplexer_1_out), .sel(Clear));
  Multiplexer #(.width(8), .enable("false")) multiplexer_2 (
    .in0(Write_Data), .in1({8{1'b1}}), .out(multiplexer_2_out), .sel(Clear));
  Multiplexer #(.enable("false")) multiplexer_3 (.in0(CLK), .in1(Clear), .out(multiplexer_3_out), .sel(Clear));
  Register_part u_zero (.D(Write_Data), .en(and_1_out), .Q(zero), .clk(CLK), .clr(Clear));
  Register_part u_t0 (.D(Write_Data), .en(and_2_out), .Q(t0), .clk(CLK), .clr(Clear));
  Register_part u_t1 (.D(Write_Data), .en(and_3_out), .Q(t1), .clk(CLK), .clr(Clear));
  Register_part u_t2 (.D(Write_Data), .en(and_4_out), .Q(t2), .clk(CLK), .clr(Clear));
  Register_part u_t3 (.D(Write_Data), .en(and_5_out), .Q(t3), .clk(CLK), .clr(Clear));
  Register_part u_t4 (.D(Write_Data), .en(and_6_out), .Q(t4), .clk(CLK), .clr(Clear));
  Register_part u_sp (.D(multiplexer_2_out), .en(multiplexer_1_out), .Q(sp), .clk(multiplexer_3_out));  // open: clr
  Multiplexer #(.select(4), .width(8), .enable("false")) multiplexer_4 (
    .in0(zero), .in1(t0), .in2(t1), .in3(t2), .in4(t3), .in5(t4), .in6(sp), .out(Read_data_1),
    .sel(Read_Register_1));  // open: in7, in8, in9, in10, in11, in12, in13, in14, in15
  Multiplexer #(.select(4), .width(8), .enable("false")) multiplexer_5 (
    .in0(zero), .in1(t0), .in2(t1), .in3(t2), .in4(t3), .in5(t4), .in6(sp), .out(Read_data_2),
    .sel(Read_Register_2));  // open: in7, in8, in9, in10, in11, in12, in13, in14, in15
endmodule

module Control (
  input  [3:0] OpCode,
  output [2:0] ALUOp,
  output ALUSrc,
  output Bneq,
  output Beq,
  output MemToReg,
  output MemWrite,
  output MemRead,
  output RegWrite,
  output RegDst,
  output Shift,
  output Jump
);

  ROM #(.addrWidth(4), .dataWidth(13)) rom_1 (
    .addr(OpCode),
    .data({Jump, Shift, RegDst, RegWrite, MemRead, MemWrite, MemToReg, Beq, Bneq, ALUSrc, ALUOp}));  // open: sel

  // Notes on the sheet:
  //   contents of rom_1 (hex, n*v repeats v):
  //   20b 208 20a e0e 600 88 348 603 604 11 1000 e0d 601 21 209 602
endmodule

module IF_ID (
  input  [19:0] Ins,
  input  clk,
  input  clr,
  output [19:0] Instruction
);

  Register_part #(.width(20)) IF_ID_REG (.D(Ins), .en(1'b1), .Q(Instruction), .clk(clk), .clr(clr));
endmodule
