// Logisim project Project_PIpelined_Reg _Fwding _Hazard_Branching.circ as structural Verilog
// IF/ID
module main (
  input  Clr,
  output [3:0] rs_reg,
  output [3:0] rt_reg,
  output Mem_write,
  output [3:0] rd_reg,
  output rw,
  output [23:0] im,
  output [19:0] Read_Adress,
  output [19:0] Read_Adress_2,
  output [7:0] PC,
  output [3:0] rs,
  output [7:0] A_Read_Data_1,
  output [3:0] rd,
  output Mem_write_2,
  output [3:0] rt,
  output Mem_read,
  output [7:0] ALU_Result,
  output [3:0] rd_reg_2,
  output [7:0] out_19,
  output [7:0] B_Read_Data_2,
  output [7:0] B,
  output [3:0] rd_reg_3,
  output [7:0] im_2,
  output [3:0] B_Read_Data_2_2,
  output [3:0] src1,
  output [7:0] zero,
  output [7:0] sp,
  output [7:0] B_Read_Data_2_3,
  output [7:0] im_3,
  output [7:0] t0,
  output [7:0] Write_Data,
  output [7:0] t4,
  output [7:0] t1,
  output [7:0] A_Read_Data_1_2,
  output [7:0] t3,
  output [3:0] src2,
  output [3:0] out_37,
  output [7:0] t2,
  output [7:0] out_39,
  output out_40,
  output [7:0] out_41,
  output [7:0] out_42,
  output out_43,
  output out_44,
  output [7:0] out_45
);

  wire be, bne, branching_fwding_ckt_1_forward_alu_result_in_rs,
       branching_fwding_ckt_1_forward_alu_result_in_rt, BranchSelect, clk, comparator_1_eq, control_1_alusrc,
       control_1_memread, control_1_memtoreg, control_1_memwrite, control_1_regdst, control_1_regwrite,
       control_1_shift, EX_MEM_RegWrite, id_ex_1_alusrc, id_ex_1_reg_destination, id_ex_1_shift,
       ID_EX_MEM_READ, ID_EX_Mem_Write, ID_EX_MemtoReg, ID_EX_Reg_Write, jump, main_3_memtoreg_rw_2,
       mem_splitter_1_b, mem_splitter_1_bn, Mem_Wb_rw, multiplexer_5_out, multiplexer_6_out, not_1_out,
       not_2_out, not_3_out, or_1_out, stall;
  wire [1:0] fwding_unit_1_fwd_a, fwding_unit_1_fwd_b;
  wire [2:0] control_1_aluop, id_ex_1_alu_op_2;
  wire [3:0] multiplexer_13_out;
  wire [5:0] id_ex_1_mem;
  wire [7:0] adder_1_out, adder_2_out, alu_fix_1_alu_a, alu_fix_1_alu_b, id_ex_1_im, id_ex_1_rs, id_ex_1_rt,
       if_id_1_nextpco, main_2_data_memory_2, main_3_data_memory_2, multiplexer_3_out, multiplexer_4_out,
       multiplexer_10_out, multiplexer_11_out, multiplexer_12_out, ram_1_data;
  wire [8:0] multiplexer_9_out, n10_1_1_out_10;

  not not_1 (not_1_out, stall);
  Clock Clock_Pulse (.out(clk));
  Multiplexer #(.width(8), .enable("false")) multiplexer_1 (
    .in0(B_Read_Data_2), .in1(ALU_Result), .out(out_41), .sel(branching_fwding_ckt_1_forward_alu_result_in_rt));
  Multiplexer #(.width(8), .enable("false")) multiplexer_2 (
    .in0(A_Read_Data_1), .in1(ALU_Result), .out(out_42), .sel(branching_fwding_ckt_1_forward_alu_result_in_rs));
  Multiplexer #(.width(8), .enable("false")) multiplexer_3 (
    .in0(adder_1_out), .in1(adder_2_out), .out(multiplexer_3_out), .sel(BranchSelect));
  Multiplexer #(.width(8), .enable("false")) multiplexer_4 (
    .in0(multiplexer_3_out), .in1(Read_Adress[15:8]), .out(multiplexer_4_out), .sel(jump));
  Register_part register_1 (.D(multiplexer_4_out), .en(not_1_out), .Q(PC), .clk(clk), .clr(Clr));
  Multiplexer #(.enable("false")) multiplexer_5 (.in0(bne), .in1(be), .out(multiplexer_5_out), .sel(comparator_1_eq));
  Comparator comparator_1 (.a(out_41), .b(out_42), .eq(comparator_1_eq));  // open: gt, lt
  Branching_Fwding_Ckt branching_fwding_ckt_1 (
    .EX_MEM_RegWrite(EX_MEM_RegWrite), .EX_MEM_Rt(rd_reg_2), .IF_ID_Rs(Read_Adress[15:12]),
    .IF_ID_Rt(Read_Adress[11:8]), .Forward_ALU_Result_in_RS(branching_fwding_ckt_1_forward_alu_result_in_rs),
    .Forward_ALU_Result_in_RT(branching_fwding_ckt_1_forward_alu_result_in_rt));
  Adder adder_1 (.a(8'h1), .b(PC), .out(adder_1_out), .cin(1'b0));  // open: cout
  ROM #(.dataWidth(20)) rom_1 (.addr(PC), .data(Read_Adress_2));  // open: sel
  not not_2 (not_2_out, stall);
  Multiplexer #(.enable("false")) multiplexer_6 (
    .in0(multiplexer_5_out), .in1(1'b0), .out(multiplexer_6_out), .sel(stall));
  Multiplexer #(.enable("false")) multiplexer_7 (.in0(multiplexer_6_out), .in1(1'b0), .out(BranchSelect), .sel(jump));
  or or_1 (or_1_out, jump, BranchSelect);
  IF_ID if_id_1 (
    .Instruction(Read_Adress_2), .Instructiono({Read_Adress[19:8], B_Read_Data_2_2, im_2[3:0]}), .in_5(clk),
    .Clr(Clr), .NextPC(adder_1_out), .NextPCo(if_id_1_nextpco), .Enable(not_2_out), .IF_FLUSH(or_1_out));
  Register register_2 (
    .Write_Data(Write_Data), .Read_Register_2(Read_Adress[11:8]), .Read_Register_1(Read_Adress[15:12]),
    .Write_Register(out_37), .CLK(clk), .Write_Signal(Mem_Wb_rw), .Clear(Clr), .zero(zero), .t0(t0), .t1(t1),
    .t2(t2), .t3(t3), .t4(t4), .sp(sp), .Read_data_1(A_Read_Data_1), .Read_data_2(B_Read_Data_2));  // open: out_9
  Control control_1 (
    .OpCode(Read_Adress[19:16]), .ALUOp(control_1_aluop), .ALUSrc(control_1_alusrc), .Bneq(bne), .Beq(be),
    .MemToReg(control_1_memtoreg), .MemWrite(control_1_memwrite), .MemRead(control_1_memread),
    .RegWrite(control_1_regwrite), .RegDst(control_1_regdst), .Shift(control_1_shift), .Jump(jump));
  Hazard_Detection_main main_1 (
    .ID_EX_MemRead(ID_EX_MEM_READ), .ID_EX_RegRt(rt_reg), .IF_ID_RegRs(Read_Adress[15:12]),
    .IF_ID_RegRt(Read_Adress[11:8]), .Load_Use_and_branch_after_load(out_40), .ID_EX_RegRd(rs_reg),
    .branch_after_after_load(out_43), .EX_MEM_RegRt(rd_reg_2), .EX_MEM_MemRead(Mem_read),
    .branch_after_add_i(out_44), .IF_ID_Be(be), .IF_ID_Bne(bne), .Stall(stall),
    .ID_EX_RegWrite(ID_EX_Reg_Write));
  Multiplexer #(.width(4), .enable("false")) multiplexer_8 (
    .in0(B_Read_Data_2_2), .in1(4'b0000), .out(im_2[7:4]), .sel(control_1_shift));
  _10_1 u_10_1_1 (
    .in_1(control_1_alusrc), .in_2(1'b0), .in_3(1'b0), .in_4(control_1_memtoreg), .in_5(control_1_memwrite),
    .in_6(control_1_memread), .in_7(control_1_regwrite), .in_8(control_1_regdst), .in_9(control_1_shift),
    .out_10(n10_1_1_out_10));
  Adder adder_2 (.a(if_id_1_nextpco), .b(im_2), .out(adder_2_out));  // open: cin, cout
  Multiplexer #(.width(9), .enable("false")) multiplexer_9 (
    .in0(n10_1_1_out_10), .in1({9{1'b0}}), .out(multiplexer_9_out), .sel(stall));
  ID_EX id_ex_1 (
    .Next_Pc(if_id_1_nextpco), .ALUSrc_BN_B_MemToReg_MW_MR_RW_RD_S(multiplexer_9_out),
    .RS_RT_RD({B_Read_Data_2_2, Read_Adress[11:8], Read_Adress[15:12]}), .Clock(clk), .CLR(Clr),
    .ALUSrc(id_ex_1_alusrc), .mem(id_ex_1_mem), .reg_destination(id_ex_1_reg_destination),
    .Shift(id_ex_1_shift), .rt_reg(rt_reg), .rd_reg(rd_reg), .rs_reg(rs_reg), .Value_of_RS(A_Read_Data_1),
    .rs(id_ex_1_rs), .Value_of_Rd_rt(B_Read_Data_2), .rt(id_ex_1_rt), .im(id_ex_1_im), .Value_of_im(im_2),
    .ALU_OP(control_1_aluop), .ALU_OP_2(id_ex_1_alu_op_2), .VALUES_RS_RD_RT_IM(im));  // open: Next_Pc_2, ALUSrc_BN_B_MemToReg_MW_MR_RW_RD_S_2, RS_RT_RD_2
  mem_splitter mem_splitter_1 (
    .BN_B_MemToReg_MW_MR_RW(id_ex_1_mem), .BN(mem_splitter_1_bn), .B(mem_splitter_1_b),
    .MemToReg(ID_EX_MemtoReg), .Mem_Write(ID_EX_Mem_Write), .Mem_Read(ID_EX_MEM_READ),
    .RegWrite(ID_EX_Reg_Write));
  Multiplexer #(.select(2), .width(8), .enable("false")) multiplexer_10 (
    .in0(id_ex_1_rs), .in1(Write_Data), .in2(ALU_Result), .in3({8{1'b0}}), .out(multiplexer_10_out),
    .sel(fwding_unit_1_fwd_a));
  Multiplexer #(.select(2), .width(8), .enable("false")) multiplexer_11 (
    .in0(id_ex_1_rt), .in1(Write_Data), .in2(ALU_Result), .in3({8{1'b0}}), .out(multiplexer_11_out),
    .sel(fwding_unit_1_fwd_b));
  Fwding_UNit fwding_unit_1 (
    .EX_MEM_RegWrite(EX_MEM_RegWrite), .EX_MEM_Destination_Reg(rd_reg_2), .ID_EX_ReadRegister1(rs_reg),
    .ID_EX_ReadRegister2(rt_reg), .MEM_WB_RegWrite(Mem_Wb_rw), .MEM_WB_Destination_Reg(out_37),
    .FWD_A(fwding_unit_1_fwd_a), .FWD_B(fwding_unit_1_fwd_b));
  Multiplexer #(.width(8), .enable("false")) multiplexer_12 (
    .in0(multiplexer_11_out), .in1(id_ex_1_im), .out(multiplexer_12_out), .sel(id_ex_1_alusrc));
  ALU_FIX alu_fix_1 (
    .A(multiplexer_10_out), .B(multiplexer_12_out), .ALU_A(alu_fix_1_alu_a), .ALU_B(alu_fix_1_alu_b),
    .Shift_Control(id_ex_1_shift));
  // ALU_8_by_ART alu_8_by_art_1: pin names not known; wires that end beside it: alu_fix_1_alu_a, alu_fix_1_alu_b, id_ex_1_alu_op_2, B
  Multiplexer #(.width(4), .enable("false")) multiplexer_13 (
    .in0(rt_reg), .in1(rd_reg), .out(multiplexer_13_out), .sel(id_ex_1_reg_destination));
  EX_MEM_Reg_Branching_main main_2 (
    .MemToReg_MW_MR_RW(id_ex_1_mem[5:2]), .BN_B(id_ex_1_mem[1:0]), .ALU_Result(B), .RD(multiplexer_13_out),
    .clear(Clr), .clock(clk), .Data_Memory(multiplexer_11_out),
    .MemToReg_MW_MR_RW_2({rw, Mem_read, Mem_write_2, Mem_write}), .ALU_Result_2(ALU_Result), .RD_2(rd_reg_2),
    .Data_Memory_2(main_2_data_memory_2), .RegWrite(EX_MEM_RegWrite));  // open: BN_B_2, Level_Adress, Zero_Flag, MemToReg, MemWrite, MemRead
  not not_3 (not_3_out, clk);
  RAM #(.bus("separate")) ram_1 (
    .addr(ALU_Result), .din(main_2_data_memory_2), .data(ram_1_data), .str(Mem_write_2), .clk(not_3_out),
    .ld(Mem_read), .clr(Clr));  // open: sel
  Multiplexer #(.width(8), .enable("false")) multiplexer_14 (
    .in0(out_19), .in1(main_3_data_memory_2), .out(Write_Data), .sel(main_3_memtoreg_rw_2));
  Mem_Wb_regi_main main_3 (
    .MemToReg_RW(Mem_write), .RW(rw), .Data_Memory(ram_1_data), .ALU_Result(ALU_Result), .RD(rd_reg_2),
    .MemToReg_RW_2(main_3_memtoreg_rw_2), .RW_2(Mem_Wb_rw), .Data_Memory_2(main_3_data_memory_2),
    .ALU_Result_2(out_19), .RD_2(out_37), .clock(clk), .clear(Clr));

  assign A_Read_Data_1_2 = A_Read_Data_1;
  assign B_Read_Data_2_3 = B_Read_Data_2;
  assign im_3 = im_2;
  assign out_39 = B_Read_Data_2;
  assign out_45 = ALU_Result;
  assign rd = B_Read_Data_2_2;
  assign rd_reg_3 = out_37;
  assign Read_Adress[7:0] = {B_Read_Data_2_2, im_2[3:0]};
  assign rs = Read_Adress[15:12];
  assign rt = Read_Adress[11:8];
  assign src1 = Read_Adress[15:12];
  assign src2 = Read_Adress[11:8];

  // Other names for the same wires on the sheet: JumpAddress[7:0] = Read_Adress[15:8]; EX_MEM_MemRead = Mem_read;
  //   EX_MEM_WriteReg = rw; dst[3:0] = out_37; Mem_Wb_rd[3:0] = out_37; EX_MEM_RegRd[3:0] = rd_reg_2;
  //   ID_EX_REG_RT[3:0] = rt_reg; ID_EX_RegRt[3:0] = rt_reg; ID_EX_RegRd[3:0] = rs_reg; ID_EX_RegRs[3:0] = rs_reg;
  //   im_t[7:0] = im_2; Read_Reg_1[7:0] = A_Read_Data_1; Read_Reg_2[7:0] = B_Read_Data_2

  // Notes on the sheet:
  //   Results :
  //   Branch Select Logic :
  //   contents of rom_1 (hex, n*v repeats v):
  //   1010a 10201 d1209 10202 d1209 10201 10301 10502 42340 40320 40430 15501 951fb a0f00 10401 56400
  //   e6601 34014 56100 e6601 b1055 56500 e6601 555a2 56500 e6601 652a2 56200 e6601 12388 56300 e6601
  //   e3481 c4340 56400 e6601 10146 10255 71230 56300 e6601 34fe 56400 e6601 10480 105aa f4520 56200 e6601
  //   223ff 56300 e6601 a3400
  //   Hazard Detection Unit:
  //   read_reg_2
  //   read_reg_1
  //   read reg2
  //   read reg1
  //   regdst
  //   rd
  //   ex stage
  //   rt
  //   rd
  //   reg.dst
  //   mem/write
  //   mem/read
  //   ALU Result
  //   ALU Result
  //   Mem_to_reg
  //   write_Register
  //   rd
  //   Mux2
  //   Data Output
  //   Made By :
  //   Fatin Ishrak Arian
  //   Roll:2105143
  //   CSE, BUET
endmodule

module Register (
  input  [3:0] Write_Register,
  input  [7:0] Write_Data,
  input  CLK,
  input  Write_Signal,
  input  Clear,
  input  [3:0] Read_Register_2,
  input  [3:0] Read_Register_1,
  output [7:0] Read_data_1,
  output [7:0] out_9,
  output [7:0] Read_data_2,
  output [7:0] sp,
  output [7:0] zero,
  output [7:0] t2,
  output [7:0] t4,
  output [7:0] t0,
  output [7:0] t3,
  output [7:0] t1
);

  wire and_1_out, and_2_out, and_3_out, and_4_out, and_5_out, and_6_out, and_7_out, and_8_out, and_9_out,
       comparator_1_eq, comparator_2_eq, decoder_1_out0, decoder_1_out1, decoder_1_out2, decoder_1_out3,
       decoder_1_out4, decoder_1_out5, decoder_1_out6, multiplexer_1_out, multiplexer_3_out;
  wire [7:0] multiplexer_2_out, multiplexer_4_out;

  Decoder #(.select(4), .enable("false")) decoder_1 (
    .out0(decoder_1_out0), .out1(decoder_1_out1), .out2(decoder_1_out2), .out3(decoder_1_out3),
    .out4(decoder_1_out4), .out5(decoder_1_out5), .out6(decoder_1_out6), .sel(Write_Register));  // open: out7, out8, out9, out10, out11, out12, out13, out14, out15
  and and_1 (and_1_out, decoder_1_out0, 1'b0);
  and and_2 (and_2_out, decoder_1_out1, Write_Signal);
  and and_3 (and_3_out, decoder_1_out2, Write_Signal);
  and and_4 (and_4_out, decoder_1_out3, Write_Signal);
  and and_5 (and_5_out, decoder_1_out4, Write_Signal);
  and and_6 (and_6_out, decoder_1_out5, Write_Signal);
  and and_7 (and_7_out, decoder_1_out6, Write_Signal);
  Multiplexer #(.enable("false")) multiplexer_1 (.in0(and_7_out), .in1(Clear), .out(multiplexer_1_out), .sel(Clear));
  Multiplexer #(.width(8), .enable("false")) multiplexer_2 (
    .in0(Write_Data), .in1({8{1'b1}}), .out(multiplexer_2_out), .sel(Clear));
  Multiplexer #(.enable("false")) multiplexer_3 (.in0(CLK), .in1(Clear), .out(multiplexer_3_out), .sel(Clear));
  Register_part u_zero (.D(Write_Data), .en(and_1_out), .Q(zero), .clk(CLK), .clr(Clear));
  Register_part u_t0 (.D(Write_Data), .en(and_2_out), .Q(t0), .clk(CLK), .clr(Clear));
  Register_part u_t1 (.D(Write_Data), .en(and_3_out), .Q(t1), .clk(CLK), .clr(Clear));
  Register_part u_t2 (.D(Write_Data), .en(and_4_out), .Q(t2), .clk(CLK), .clr(Clear));
  Register_part u_t3 (.D(Write_Data), .en(and_5_out), .Q(t3), .clk(CLK), .clr(Clear));
  Register_part u_t4 (.D(Write_Data), .en(and_6_out), .Q(t4), .clk(CLK), .clr(Clear));
  Register_part u_sp (.D(multiplexer_2_out), .en(multiplexer_1_out), .Q(sp), .clk(multiplexer_3_out));  // open: clr
  Multiplexer #(.select(4), .width(8), .enable("false")) multiplexer_4 (
    .in0(zero), .in1(t0), .in2(t1), .in3(t2), .in4(t3), .in5(t4), .in6(sp), .out(multiplexer_4_out),
    .sel(Read_Register_1));  // open: in7, in8, in9, in10, in11, in12, in13, in14, in15
  Multiplexer #(.select(4), .width(8), .enable("false")) multiplexer_5 (
    .in0(zero), .in1(t0), .in2(t1), .in3(t2), .in4(t3), .in5(t4), .in6(sp), .out(out_9), .sel(Read_Register_2));  // open: in7, in8, in9, in10, in11, in12, in13, in14, in15
  Multiplexer #(.width(8), .enable("false")) multiplexer_6 (
    .in0(multiplexer_4_out), .in1(Write_Data), .out(Read_data_1), .sel(and_8_out));
  and and_8 (and_8_out, comparator_1_eq, Write_Signal);
  Comparator #(.width(4)) comparator_1 (.a(Read_Register_1), .b(Write_Register), .eq(comparator_1_eq));  // open: gt, lt
  Multiplexer #(.width(8), .enable("false")) multiplexer_7 (
    .in0(out_9), .in1(Write_Data), .out(Read_data_2), .sel(and_9_out));
  and and_9 (and_9_out, comparator_2_eq, Write_Signal);
  Comparator #(.width(4)) comparator_2 (.a(Read_Register_2), .b(Write_Register), .eq(comparator_2_eq));  // open: gt, lt

  // Other names for the same wires on the sheet: Data[7:0] = Write_Data; destination[3:0] = Write_Register
endmodule

module Control (
  input  [3:0] OpCode,
  output [2:0] ALUOp,
  output ALUSrc,
  output Bneq,
  output Beq,
  output MemToReg,
  output MemWrite,
  output MemRead,
  output RegWrite,
  output RegDst,
  output Shift,
  output Jump
);

  ROM #(.addrWidth(4), .dataWidth(13)) rom_1 (
    .addr(OpCode),
    .data({Jump, Shift, RegDst, RegWrite, MemRead, MemWrite, MemToReg, Beq, Bneq, ALUSrc, ALUOp}));  // open: sel

  // Notes on the sheet:
  //   contents of rom_1 (hex, n*v repeats v):
  //   20b 208 20a e0e 600 88 348 603 604 11 1000 e0d 601 21 209 602
endmodule

module IF_ID (
  input  [7:0] NextPC,
  input  [19:0] Instruction,
  input  Enable,
  input  IF_FLUSH,
  input  in_5,
  input  Clr,
  output [7:0] NextPCo,
  output [19:0] Instructiono
);

  wire [7:0] multiplexer_2_out;
  wire [19:0] multiplexer_1_out;

  Multiplexer #(.width(20), .enable("false")) multiplexer_1 (
    .in0(Instruction), .in1({20{1'b0}}), .out(multiplexer_1_out), .sel(IF_FLUSH));
  Multiplexer #(.width(8), .enable("false")) multiplexer_2 (
    .in0(NextPC), .in1({8{1'b0}}), .out(multiplexer_2_out), .sel(IF_FLUSH));
  Register_part #(.width(28)) register_1 (
    .D({multiplexer_1_out, multiplexer_2_out}), .en(Enable), .Q({Instructiono, NextPCo}), .clk(in_5),
    .clr(Clr));
endmodule

module ALU_FIX (
  input  Shift_Control,
  input  [7:0] A,
  input  [7:0] B,
  output [7:0] ALU_B,
  output [7:0] ALU_A
);

  Multiplexer #(.width(8), .enable("false")) multiplexer_1 (.in0(A), .in1(B), .out(ALU_A), .sel(Shift_Control));
  Multiplexer #(.width(8), .enable("false")) multiplexer_2 (.in0(B), .in1(A), .out(ALU_B), .sel(Shift_Control));
endmodule

module _10_1 (
  input  in_1,
  input  in_2,
  input  in_3,
  input  in_4,
  input  in_5,
  input  in_6,
  input  in_7,
  input  in_8,
  input  in_9,
  output [8:0] out_10
);


  assign out_10 = {in_9, in_8, in_7, in_6, in_5, in_4, in_3, in_2, in_1};
endmodule

// mem_controls_splitter
module mem_splitter (
  input  [5:0] BN_B_MemToReg_MW_MR_RW,
  output BN,
  output B,
  output MemToReg,
  output Mem_Write,
  output Mem_Read,
  output RegWrite
);


  assign B = BN_B_MemToReg_MW_MR_RW[1];
  assign BN = BN_B_MemToReg_MW_MR_RW[0];
  assign Mem_Read = BN_B_MemToReg_MW_MR_RW[4];
  assign Mem_Write = BN_B_MemToReg_MW_MR_RW[3];
  assign MemToReg = BN_B_MemToReg_MW_MR_RW[2];
  assign RegWrite = BN_B_MemToReg_MW_MR_RW[5];
endmodule

module Branching_Fwding_Ckt (
  input  EX_MEM_RegWrite,
  input  [3:0] EX_MEM_Rt,
  input  [3:0] IF_ID_Rs,
  input  [3:0] IF_ID_Rt,
  output Forward_ALU_Result_in_RS,
  output Forward_ALU_Result_in_RT
);

  wire comparator_1_eq, comparator_2_eq;

  Comparator #(.width(4)) comparator_1 (.a(EX_MEM_Rt), .b(IF_ID_Rt), .eq(comparator_1_eq));  // open: gt, lt
  Comparator #(.width(4)) comparator_2 (.a(EX_MEM_Rt), .b(IF_ID_Rs), .eq(comparator_2_eq));  // open: gt, lt
  and and_1 (Forward_ALU_Result_in_RS, EX_MEM_RegWrite, comparator_2_eq);
  and and_2 (Forward_ALU_Result_in_RT, EX_MEM_RegWrite, comparator_1_eq);

  // Notes on the sheet:
  //   load er value o jacche
endmodule

module load_store_fwding (
  input  EX_MEM_WriteReg,
  input  EX_MEM_MemRead,
  input  ID_EX_MemWrite,
  input  [3:0] ID_EX_RT,
  input  [3:0] EX_MEM_RT,
  input  Mem_WB_RW,
  input  [3:0] MEM_WB_RT,
  output [1:0] Forward
);

  wire and_2_out, and_3_out, and_4_out, comparator_1_eq, comparator_2_eq, not_1_out;

  Comparator #(.width(4)) comparator_1 (.a(ID_EX_RT), .b(EX_MEM_RT), .eq(comparator_1_eq));  // open: gt, lt
  not not_1 (not_1_out, Forward[1]);
  Comparator #(.width(4)) comparator_2 (.a(ID_EX_RT), .b(MEM_WB_RT), .eq(comparator_2_eq));  // open: gt, lt
  and and_1 (Forward[1], EX_MEM_WriteReg, ID_EX_MemWrite, comparator_1_eq);
  and and_2 (and_2_out, not_1_out, ID_EX_MemWrite, comparator_2_eq);
  and and_3 (and_3_out, EX_MEM_MemRead, Forward[1]);
  or or_1 (Forward[0], and_3_out, and_4_out);
  and and_4 (and_4_out, Mem_WB_RW, and_2_out);
endmodule
