// Logisim project Project_PIpelined_Reg _Fwding.circ as structural Verilog
// IF/ID
module main (
  input  Clr,
  output [19:0] Read_Adress,
  output [23:0] im,
  output [19:0] Read_Adress_2,
  output [7:0] PC,
  output [7:0] A_Read_Data_1,
  output [7:0] B,
  output [7:0] out_8,
  output [7:0] B_Read_Data_2,
  output [7:0] B_2,
  output [7:0] im_2,
  output [3:0] B_Read_Data_2_2,
  output [3:0] src1,
  output [3:0] src2,
  output [3:0] out_15,
  output [7:0] zero,
  output [7:0] sp,
  output [7:0] t0,
  output [7:0] Write_Data,
  output [7:0] t4,
  output [7:0] t1,
  output [7:0] t3,
  output [7:0] t2
);

  wire alu_8_by_art_1_p4, and_1_out, and_2_out, clk, control_1_alusrc, control_1_beq, control_1_bneq,
       control_1_jump, control_1_memread, control_1_memtoreg, control_1_memwrite, control_1_regdst,
       control_1_regwrite, control_1_shift, id_ex_1_alusrc, id_ex_1_reg_destination, id_ex_1_shift,
       main_1_regwrite, main_1_zero_flag_2, main_2_memtoreg_rw_2, Mem_Wb_rw, not_1_out, not_2_out;
  wire [1:0] main_1_bn_b_2, priority_encoder_1_out;
  wire [2:0] control_1_aluop, id_ex_1_alu_op_2;
  wire [3:0] id_ex_1_rd_reg, id_ex_1_rs_reg, id_ex_1_rt_reg, main_1_memtoreg_mw_mr_rw_2, main_1_rd_2,
       multiplexer_5_out;
  wire [5:0] id_ex_1_mem;
  wire [7:0] adder_2_out, alu_fix_1_alu_a, alu_fix_1_alu_b, id_ex_1_im, id_ex_1_next_pc_2, id_ex_1_rs,
       id_ex_1_rt, if_id_1_nextpco, main_1_data_memory_2, main_1_level_adress, main_2_data_memory_2,
       multiplexer_2_out, multiplexer_3_out, multiplexer_4_out, MUX1_INP_0_PC_1, PC_FInal_Address, ram_1_data;
  wire [8:0] n10_1_1_out_10;

  Clock Clock_Pulse (.out(clk));
  Register_part register_1 (.D(PC_FInal_Address), .Q(PC), .clk(clk), .clr(Clr));  // open: en
  Adder adder_1 (.a(8'h1), .b(PC), .out(MUX1_INP_0_PC_1), .cin(1'b0));  // open: cout
  ROM #(.dataWidth(20)) rom_1 (.addr(PC), .data(Read_Adress_2));  // open: sel
  IF_ID if_id_1 (
    .Instruction(Read_Adress_2), .Instructiono({Read_Adress[19:8], B_Read_Data_2_2, im_2[3:0]}), .in_3(clk),
    .Clr(Clr), .NextPC(MUX1_INP_0_PC_1), .NextPCo(if_id_1_nextpco));
  Register register_2 (
    .Write_Data(Write_Data), .Read_Register_2(Read_Adress[11:8]), .Read_Register_1(Read_Adress[15:12]),
    .Write_Register(out_15), .CLK(clk), .Write_Signal(Mem_Wb_rw), .Clear(Clr), .zero(zero), .t0(t0), .t1(t1),
    .t2(t2), .t3(t3), .t4(t4), .sp(sp), .Read_data_1(A_Read_Data_1), .Read_data_2(B_Read_Data_2));
  Control control_1 (
    .OpCode(Read_Adress[19:16]), .ALUOp(control_1_aluop), .ALUSrc(control_1_alusrc), .Bneq(control_1_bneq),
    .Beq(control_1_beq), .MemToReg(control_1_memtoreg), .MemWrite(control_1_memwrite),
    .MemRead(control_1_memread), .RegWrite(control_1_regwrite), .RegDst(control_1_regdst),
    .Shift(control_1_shift), .Jump(control_1_jump));
  Multiplexer #(.width(4), .enable("false")) multiplexer_1 (
    .in0(B_Read_Data_2_2), .in1(4'b0000), .out(im_2[7:4]), .sel(id_ex_1_shift));
  _10_1 u_10_1_1 (
    .in_1(control_1_alusrc), .in_2(control_1_bneq), .in_3(control_1_beq), .in_4(control_1_memtoreg),
    .in_5(control_1_memwrite), .in_6(control_1_memread), .in_7(control_1_regwrite), .in_8(control_1_regdst),
    .in_9(control_1_shift), .out_10(n10_1_1_out_10));
  ID_EX id_ex_1 (
    .Next_Pc(if_id_1_nextpco), .ALUSrc_BN_B_MemToReg_MW_MR_RW_RD_S(n10_1_1_out_10),
    .RS_RT_RD({B_Read_Data_2_2, Read_Adress[11:8], Read_Adress[15:12]}),
    .VALUES_RS_RD_RT_IM({im_2, B_Read_Data_2, A_Read_Data_1}), .ALU_OP(control_1_aluop), .Clock(clk),
    .CLR(Clr), .Next_Pc_2(id_ex_1_next_pc_2), .VALUES_RS_RD_RT_IM_2(im), .ALU_OP_2(id_ex_1_alu_op_2),
    .ALUSrc(id_ex_1_alusrc), .mem(id_ex_1_mem), .reg_destination(id_ex_1_reg_destination),
    .Shift(id_ex_1_shift), .rs(id_ex_1_rs), .rt(id_ex_1_rt), .im(id_ex_1_im), .rt_reg(id_ex_1_rt_reg),
    .rd_reg(id_ex_1_rd_reg), .rs_reg(id_ex_1_rs_reg));  // open: ALUSrc_BN_B_MemToReg_MW_MR_RW_RD_S_2, RS_RT_RD_2
  Adder adder_2 (.a(id_ex_1_next_pc_2), .b(im_2), .out(adder_2_out));  // open: cin, cout
  Multiplexer #(.select(2), .width(8), .enable("false")) multiplexer_2 (
    .in0(id_ex_1_rs), .in1(Write_Data), .in2(B), .in3({8{1'b0}}), .out(multiplexer_2_out));  // open: sel
  Multiplexer #(.select(2), .width(8), .enable("false")) multiplexer_3 (
    .in0(id_ex_1_rt), .in1(Write_Data), .in2(B), .in3({8{1'b0}}), .out(multiplexer_3_out));  // open: sel
  Fwding_UNit fwding_unit_1 (
    .EX_MEM_RegWrite(main_1_regwrite), .EX_MEM_Destination_Reg(main_1_rd_2),
    .ID_EX_ReadRegister1(id_ex_1_rs_reg), .ID_EX_ReadRegister2(id_ex_1_rt_reg), .MEM_WB_RegWrite(Mem_Wb_rw),
    .MEM_WB_Destination_Reg(out_15));  // open: FWD_A, FWD_B
  Multiplexer #(.width(8), .enable("false")) multiplexer_4 (
    .in0(multiplexer_3_out), .in1(id_ex_1_im), .out(multiplexer_4_out), .sel(id_ex_1_alusrc));
  ALU_FIX alu_fix_1 (
    .A(multiplexer_2_out), .B(multiplexer_4_out), .ALU_A(alu_fix_1_alu_a), .ALU_B(alu_fix_1_alu_b),
    .Shift_Control(id_ex_1_shift));
  // ALU_8_by_ART alu_8_by_art_1: pin names not known; wires that end beside it: alu_fix_1_alu_a, alu_fix_1_alu_b, id_ex_1_alu_op_2, alu_8_by_art_1_p4, B_2
  Multiplexer #(.width(4), .enable("false")) multiplexer_5 (
    .in0(id_ex_1_rt_reg), .in1(id_ex_1_rd_reg), .out(multiplexer_5_out), .sel(id_ex_1_reg_destination));
  EX_MEM_Regi_main main_1 (
    .MemToReg_MW_MR_RW(id_ex_1_mem[5:2]), .BN_B(id_ex_1_mem[1:0]), .Label_Address(adder_2_out),
    .Zero_flag(alu_8_by_art_1_p4), .ALU_Result(B_2), .RD(multiplexer_5_out), .clear(Clr), .clock(clk),
    .Data_Memory(id_ex_1_rt), .MemToReg_MW_MR_RW_2(main_1_memtoreg_mw_mr_rw_2), .BN_B_2(main_1_bn_b_2),
    .Level_Adress(main_1_level_adress), .Zero_Flag_2(main_1_zero_flag_2), .ALU_Result_2(B),
    .RD_2(main_1_rd_2), .Data_Memory_2(main_1_data_memory_2), .RegWrite(main_1_regwrite));  // open: MemToReg, MemWrite, MemRead
  not not_1 (not_1_out, main_1_zero_flag_2);
  and and_1 (and_1_out, main_1_bn_b_2[0], not_1_out);
  and and_2 (and_2_out, main_1_bn_b_2[1], main_1_zero_flag_2);
  Priority_Encoder #(.select(2)) priority_encoder_1 (
    .in0(1'b1), .in1(and_1_out), .in2(and_2_out), .in3(control_1_jump), .out(priority_encoder_1_out));  // open: gs, en_out, en_in
  Multiplexer #(.select(2), .width(8), .enable("false")) multiplexer_6 (
    .in0(MUX1_INP_0_PC_1), .in1(main_1_level_adress), .in2(main_1_level_adress), .in3(Read_Adress[15:8]),
    .out(PC_FInal_Address), .sel(priority_encoder_1_out));
  not not_2 (not_2_out, clk);
  RAM #(.bus("separate")) ram_1 (
    .addr(B), .din(main_1_data_memory_2), .data(ram_1_data), .str(main_1_memtoreg_mw_mr_rw_2[1]),
    .clk(not_2_out), .ld(main_1_memtoreg_mw_mr_rw_2[2]), .clr(Clr));  // open: sel
  Multiplexer #(.width(8), .enable("false")) multiplexer_7 (
    .in0(out_8), .in1(main_2_data_memory_2), .out(Write_Data), .sel(main_2_memtoreg_rw_2));
  Mem_Wb_regi_main main_2 (
    .MemToReg_RW(main_1_memtoreg_mw_mr_rw_2[0]), .RW(main_1_memtoreg_mw_mr_rw_2[3]),
    .Data_Memory(ram_1_data), .ALU_Result(B), .RD(main_1_rd_2), .MemToReg_RW_2(main_2_memtoreg_rw_2),
    .RW_2(Mem_Wb_rw), .Data_Memory_2(main_2_data_memory_2), .ALU_Result_2(out_8), .RD_2(out_15), .clock(clk),
    .clear(Clr));

  assign Read_Adress[7:0] = {B_Read_Data_2_2, im_2[3:0]};
  assign src1 = Read_Adress[15:12];
  assign src2 = Read_Adress[11:8];

  // Other names for the same wires on the sheet: MUX1_INP_3_Branch[7:0] = Read_Adress[15:8]; dst[3:0] = out_15

  // Notes on the sheet:
  //   Results
  //   contents of rom_1 (hex, n*v repeats v):
  //   1020a 10305 42300 41340 42150 53203 b2021 d3301 a1500 c5150 e2202 34041 63203 72410 f1530 a1400
  //   21105 3314 83330 a1500 913fb
  //   read reg2
  //   read reg1
  //   regdst
  //   Adder 1
  //   rd
  //   ex stage
  //   mem/write
  //   mem/read
  //   MUX1
  //   ALU Result
  //   ALU Result
  //   Mem_to_reg
  //   rw
  //   rd
  //   Mux2
  //   Data Output
endmodule

module Register (
  input  [3:0] Write_Register,
  input  [7:0] Write_Data,
  input  CLK,
  input  Write_Signal,
  input  Clear,
  input  [3:0] Read_Register_2,
  input  [3:0] Read_Register_1,
  output [7:0] Read_data_1,
  output [7:0] Read_data_2,
  output [7:0] sp,
  output [7:0] zero,
  output [7:0] t2,
  output [7:0] t4,
  output [7:0] t0,
  output [7:0] t3,
  output [7:0] t1
);

  wire and_1_out, and_2_out, and_3_out, and_4_out, and_5_out, and_6_out, and_7_out, decoder_1_out0,
       decoder_1_out1, decoder_1_out2, decoder_1_out3, decoder_1_out4, decoder_1_out5, decoder_1_out6,
       multiplexer_1_out, multiplexer_3_out;
  wire [7:0] multiplexer_2_out;

  Decoder #(.select(4), .enable("false")) decoder_1 (
    .out0(decoder_1_out0), .out1(decoder_1_out1), .out2(decoder_1_out2), .out3(decoder_1_out3),
    .out4(decoder_1_out4), .out5(decoder_1_out5), .out6(decoder_1_out6), .sel(Write_Register));  // open: out7, out8, out9, out10, out11, out12, out13, out14, out15
  and and_1 (and_1_out, decoder_1_out0, 1'b0);
  and and_2 (and_2_out, decoder_1_out1, Write_Signal);
  and and_3 (and_3_out, decoder_1_out2, Write_Signal);
  and and_4 (and_4_out, decoder_1_out3, Write_Signal);
  and and_5 (and_5_out, decoder_1_out4, Write_Signal);
  and and_6 (and_6_out, decoder_1_out5, Write_Signal);
  and and_7 (and_7_out, decoder_1_out6, Write_Signal);
  Multiplexer #(.enable("false")) multiplexer_1 (.in0(and_7_out), .in1(Clear), .out(multiplexer_1_out), .sel(Clear));
  Multiplexer #(.width(8), .enable("false")) multiplexer_2 (
    .in0(Write_Data), .in1({8{1'b1}}), .out(multiplexer_2_out), .sel(Clear));
  Multiplexer #(.enable("false")) multiplexer_3 (.in0(CLK), .in1(Clear), .out(multiplexer_3_out), .sel(Clear));
  Register_part u_zero (.D(Write_Data), .en(and_1_out), .Q(zero), .clk(CLK), .clr(Clear));
  Register_part u_t0 (.D(Write_Data), .en(and_2_out), .Q(t0), .clk(CLK), .clr(Clear));
  Register_part u_t1 (.D(Write_Data), .en(and_3_out), .Q(t1), .clk(CLK), .clr(Clear));
  Register_part u_t2 (.D(Write_Data), .en(and_4_out), .Q(t2), .clk(CLK), .clr(Clear));
  Register_part u_t3 (.D(Write_Data), .en(and_5_out), .Q(t3), .clk(CLK), .clr(Clear));
  Register_part u_t4 (.D(Write_Data), .en(and_6_out), .Q(t4), .clk(CLK), .clr(Clear));
  Register_part u_sp (.D(multiplexer_2_out), .en(multiplexer_1_out), .Q(sp), .clk(multiplexer_3_out));  // open: clr
  Multiplexer #(.select(4), .width(8), .enable("false")) multiplexer_4 (
    .in0(zero), .in1(t0), .in2(t1), .in3(t2), .in4(t3), .in5(t4), .in6(sp), .out(Read_data_1),
    .sel(Read_Register_1));  // open: in7, in8, in9, in10, in11, in12, in13, in14, in15
  Multiplexer #(.select(4), .width(8), .enable("false")) multiplexer_5 (
    .in0(zero), .in1(t0), .in2(t1), .in3(t2), .in4(t3), .in5(t4), .in6(sp), .out(Read_data_2),
    .sel(Read_Register_2));  // open: in7, in8, in9, in10, in11, in12, in13, in14, in15
endmodule

module Control (
  input  [3:0] OpCode,
  output [2:0] ALUOp,
  output ALUSrc,
  output Bneq,
  output Beq,
  output MemToReg,
  output MemWrite,
  output MemRead,
  output RegWrite,
  output RegDst,
  output Shift,
  output Jump
);

  ROM #(.addrWidth(4), .dataWidth(13)) rom_1 (
    .addr(OpCode),
    .data({Jump, Shift, RegDst, RegWrite, MemRead, MemWrite, MemToReg, Beq, Bneq, ALUSrc, ALUOp}));  // open: sel

  // Notes on the sheet:
  //   contents of rom_1 (hex, n*v repeats v):
  //   20b 208 20a e0e 600 88 348 603 604 11 1000 e0d 601 21 209 602
endmodule

module IF_ID (
  input  [7:0] NextPC,
  input  [19:0] Instruction,
  input  in_3,
  input  Clr,
  output [7:0] NextPCo,
  output [19:0] Instructiono
);

  Register_part #(.width(28)) register_1 (
    .D({Instruction, NextPC}), .en(1'b1), .Q({Instructiono, NextPCo}), .clk(in_3), .clr(Clr));
endmodule

module ALU_FIX (
  input  Shift_Control,
  input  [7:0] A,
  input  [7:0] B,
  output [7:0] ALU_B,
  output [7:0] ALU_A
);

  Multiplexer #(.width(8), .enable("false")) multiplexer_1 (.in0(A), .in1(B), .out(ALU_A), .sel(Shift_Control));
  Multiplexer #(.width(8), .enable("false")) multiplexer_2 (.in0(B), .in1(A), .out(ALU_B), .sel(Shift_Control));
endmodule

module _10_1 (
  input  in_1,
  input  in_2,
  input  in_3,
  input  in_4,
  input  in_5,
  input  in_6,
  input  in_7,
  input  in_8,
  input  in_9,
  output [8:0] out_10
);


  assign out_10 = {in_9, in_8, in_7, in_6, in_5, in_4, in_3, in_2, in_1};
endmodule
