// Logisim project rightShifterLib.circ as structural Verilog
// 1
module _1_bit_rightShifter (
  input  [31:0] in_1,
  input  in_2,
  output [31:0] out_3
);

  Multiplexer #(.width(32)) multiplexer_1 (.in0(in_1), .in1({1'b0, in_1[31:1]}), .out(out_3), .sel(in_2), .en(1'b1));
endmodule

// 2
module _2_bit_rightShifter (
  input  [31:0] in_1,
  input  in_2,
  output [31:0] out_3
);

  Multiplexer #(.width(32)) multiplexer_1 (.in0(in_1), .in1({2'b00, in_1[31:2]}), .out(out_3), .sel(in_2), .en(1'b1));
endmodule

// 4
module _4_bit_rightShifter (
  input  [31:0] in_1,
  input  in_2,
  output [31:0] out_3
);

  Multiplexer #(.width(32)) multiplexer_1 (.in0(in_1), .in1({4'b0000, in_1[31:4]}), .out(out_3), .sel(in_2), .en(1'b1));
endmodule

// 8
module _8_bit_rightShifter (
  input  [31:0] in_1,
  input  in_2,
  output [31:0] out_3
);

  Multiplexer #(.width(32)) multiplexer_1 (
    .in0(in_1), .in1({{8{1'b0}}, in_1[31:8]}), .out(out_3), .sel(in_2), .en(1'b1));
endmodule

// 16
module _16_bit_rightShifter (
  input  [31:0] in_1,
  input  in_2,
  output [31:0] out_3
);

  Multiplexer #(.width(32)) multiplexer_1 (
    .in0(in_1), .in1({{16{1'b0}}, in_1[31:16]}), .out(out_3), .sel(in_2), .en(1'b1));
endmodule

// 32
module _32_bit_rightShifter (
  input  [31:0] in_1,
  input  in_2,
  output [31:0] out_3
);

  Multiplexer #(.width(32)) multiplexer_1 (.in0(in_1), .in1({32{1'b0}}), .out(out_3), .sel(in_2), .en(1'b1));
endmodule

// ARS
module arbitary_rightShifter (
  input  [31:0] \input ,
  input  [4:0] Shift_Amount,
  output [31:0] \output 
);

  wire [31:0] n1_bit_rightshifter_1_out_3, n2_bit_rightshifter_1_out_3, n4_bit_rightshifter_1_out_3,
       n8_bit_rightshifter_1_out_3;

  _1_bit_rightShifter u_1_bit_rightshifter_1 (
    .in_1(\input ), .in_2(Shift_Amount[0]), .out_3(n1_bit_rightshifter_1_out_3));
  _2_bit_rightShifter u_2_bit_rightshifter_1 (
    .in_1(n1_bit_rightshifter_1_out_3), .in_2(Shift_Amount[1]), .out_3(n2_bit_rightshifter_1_out_3));
  _4_bit_rightShifter u_4_bit_rightshifter_1 (
    .in_1(n2_bit_rightshifter_1_out_3), .in_2(Shift_Amount[2]), .out_3(n4_bit_rightshifter_1_out_3));
  _8_bit_rightShifter u_8_bit_rightshifter_1 (
    .in_1(n4_bit_rightshifter_1_out_3), .in_2(Shift_Amount[3]), .out_3(n8_bit_rightshifter_1_out_3));
  _16_bit_rightShifter u_16_bit_rightshifter_1 (
    .in_1(n8_bit_rightshifter_1_out_3), .in_2(Shift_Amount[4]), .out_3(\output ));
endmodule

module rightShifter (
  input  [31:0] significand,
  input  [10:0] exponent_difference,
  output [31:0] \output 
);

  wire dip_7432_1_p2, dip_7432_1_p3, dip_7432_1_p4, dip_7432_2_p2, dip_7432_2_p6;
  wire [31:0] arbitary_rightshifter_1_output;

  // DIP_7432 dip_7432_1: pin names not known; wires that end beside it: exponent_difference[10], dip_7432_1_p2, dip_7432_1_p3, dip_7432_1_p4, exponent_difference[9], dip_7432_1_p2
  arbitary_rightShifter arbitary_rightshifter_1 (
    .\input (significand), .Shift_Amount(exponent_difference[4:0]), .\output (arbitary_rightshifter_1_output));
  // DIP_7432 dip_7432_2: pin names not known; wires that end beside it: exponent_difference[8], dip_7432_2_p2, dip_7432_1_p4, exponent_difference[5], exponent_difference[6], dip_7432_2_p6, dip_7432_2_p6, exponent_difference[7], dip_7432_2_p2
  Multiplexer #(.width(32)) multiplexer_1 (
    .in0(arbitary_rightshifter_1_output), .in1({32{1'b0}}), .out(\output ), .sel(dip_7432_1_p3), .en(1'b1));
endmodule
